// Logisim project 1801CS31_A2.circ as structural Verilog: 3 circuits, main circuit main
module main (
  input  [1:0] in_1,
  input  [1:0] in_2
);

  wire Clock, comparator_1_eq, comparator_3_eq, comparator_4_eq, comparator_5_eq, comparator_6_eq, Reset;
  wire [3:0] display_driver_1_out_6, display_driver_1_out_7, display_driver_1_out_8, multiplexer_1_out,
       multiplexer_2_out, next_state, state;
  wire [7:0] Total_Votes, Votes_1, Votes_2, Votes_3;

  Comparator #(.width(4)) comparator_1 (.a(state), .b(4'b0001), .eq(comparator_1_eq));  // open: gt, lt
  Comparator #(.width(4)) comparator_2 (.a(state), .b(4'b0100), .eq(Reset));  // open: gt, lt
  Multiplexer #(.select(2), .width(4)) multiplexer_1 (
    .in0(4'b0101), .in1(4'b0110), .in2(4'b0111), .out(multiplexer_1_out), .sel(in_2), .en(comparator_1_eq));  // open: in3
  Multiplexer #(.select(2), .width(4)) multiplexer_2 (
    .in0(4'b0001), .in1(4'b0010), .in2(4'b0011), .in3(4'b0100), .out(multiplexer_2_out), .sel(in_1),
    .en(comparator_3_eq));
  Comparator #(.width(4)) comparator_3 (.a(state), .b(4'b0000), .eq(comparator_3_eq));  // open: gt, lt
  Button button_1 (.out(Clock));
  Multiplexer #(.select(4), .width(4)) multiplexer_3 (
    .in0(multiplexer_2_out), .in1(multiplexer_1_out), .in2(4'b0000), .in3(4'b1000), .in4(4'b0000),
    .in5(4'b0000), .in6(4'b0000), .in7(4'b0000), .in8(4'b1001), .in9(4'b0000), .out(next_state), .sel(state));  // open: in10, in11, in12, in13, in14, in15, en
  Register #(.width(4)) register_1 (.D(next_state), .Q(state), .clk(Clock), .clr(Reset));  // open: en
  Comparator #(.width(4)) comparator_4 (.a(next_state), .b(4'b0101), .eq(comparator_4_eq));  // open: gt, lt
  Comparator #(.width(4)) comparator_5 (.a(next_state), .b(4'b0110), .eq(comparator_5_eq));  // open: gt, lt
  Comparator #(.width(4)) comparator_6 (.a(next_state), .b(4'b0111), .eq(comparator_6_eq));  // open: gt, lt
  Counter counter_1 (.count(comparator_4_eq), .Q(Votes_1), .clk(Clock), .clr(Reset));  // open: load, D, carry
  Counter counter_2 (.count(comparator_5_eq), .Q(Votes_2), .clk(Clock), .clr(Reset));  // open: load, D, carry
  Counter counter_3 (.count(comparator_6_eq), .Q(Votes_3), .clk(Clock), .clr(Reset));  // open: load, D, carry
  Hex_Digit_Display hex_digit_display_1 (.value(display_driver_1_out_6));  // open: dp
  Hex_Digit_Display hex_digit_display_2 (.value(display_driver_1_out_7));  // open: dp
  Display_Driver display_driver_1 (
    .Total_Votes(Total_Votes), .Votes_1(Votes_1), .Votes_2(Votes_2), .Votes_3(Votes_3), .State(state),
    .out_6(display_driver_1_out_6), .out_7(display_driver_1_out_7), .out_8(display_driver_1_out_8));
  _3_8_bit_adder u_3_8_bit_adder_1 (.in_1(Votes_1), .in_2(Votes_2), .in_3(Votes_3), .out_4(Total_Votes));
  Hex_Digit_Display hex_digit_display_3 (.value(display_driver_1_out_8));  // open: dp

  // Other names for the same wires on the sheet: Select_Task[1:0] = in_1; Vote[1:0] = in_2

  // Notes on the sheet:
  //   State Register
  //   Votes Cast for Candidate 1
  //   Votes Cast for Candidate 2
  //   Votes Cast for Candidate 3
  //   Display Driver
  //   Display
  //   Total Votes Cast
endmodule

module Display_Driver (
  input  [7:0] Total_Votes,
  input  [7:0] Votes_1,
  input  [7:0] Votes_2,
  input  [7:0] Votes_3,
  input  [3:0] State,
  output [3:0] out_6,
  output [3:0] out_7,
  output [3:0] out_8
);

  Multiplexer #(.select(4), .width(4)) multiplexer_1 (
    .in3(4'b0001), .in8(4'b0010), .in9(4'b0011), .out(out_6), .sel(State));  // open: in0, in1, in2, in4, in5, in6, in7, in10, in11, in12, in13, in14, in15, en
  Multiplexer #(.select(4), .width(8)) multiplexer_2 (
    .in2(Total_Votes), .in3(Votes_1), .in8(Votes_2), .in9(Votes_3), .out({out_7, out_8}), .sel(State));  // open: in0, in1, in4, in5, in6, in7, in10, in11, in12, in13, in14, in15, en
endmodule

module _3_8_bit_adder (
  input  [7:0] in_1,
  input  [7:0] in_2,
  input  [7:0] in_3,
  output [7:0] out_4
);

  wire adder_1_cout;
  wire [7:0] adder_1_out;

  Adder adder_1 (.a(in_1), .b(in_2), .out(adder_1_out), .cout(adder_1_cout));  // open: cin
  Adder adder_2 (.a(adder_1_out), .b(in_3), .out(out_4), .cin(adder_1_cout));  // open: cout
endmodule
