// Logisim project 1801CS31_A3.circ as structural Verilog: 1 circuit, main circuit main
module main (
  input  [19:0] _20_bit_Sequence,
  input  Load,
  input  Clock,
  input  Reset,
  input  [3:0] Pattern_for_Detection,
  output [3:0] Last_4_bits,
  output Output
);

  wire Remaining_Bits_out, xnor_1_out, xnor_2_out, xnor_3_out, xnor_4_out;

  Shift_Register #(.length(20)) Remaining_Bits (
    .clk(Clock), .out(Remaining_Bits_out), .load(Load), .clr(Reset), .d0(_20_bit_Sequence[0]),
    .d1(_20_bit_Sequence[1]), .d2(_20_bit_Sequence[2]), .d3(_20_bit_Sequence[3]), .d4(_20_bit_Sequence[4]),
    .d5(_20_bit_Sequence[5]), .d6(_20_bit_Sequence[6]), .d7(_20_bit_Sequence[7]), .d8(_20_bit_Sequence[8]),
    .d9(_20_bit_Sequence[9]), .d10(_20_bit_Sequence[10]), .d11(_20_bit_Sequence[11]),
    .d12(_20_bit_Sequence[12]), .d13(_20_bit_Sequence[13]), .d14(_20_bit_Sequence[14]),
    .d15(_20_bit_Sequence[15]), .d16(_20_bit_Sequence[16]), .d17(_20_bit_Sequence[17]),
    .d18(_20_bit_Sequence[18]), .d19(_20_bit_Sequence[19]));  // open: shift, in, q0, q1, q2, q3, q4, q5, q6, q7, q8, q9, q10, q11, q12, q13, q14, q15, q16, q17, q18, q19
  Shift_Register #(.length(4)) Temp (
    .in(Remaining_Bits_out), .clk(Clock), .clr(Reset), .q0(Last_4_bits[0]), .q1(Last_4_bits[1]),
    .q2(Last_4_bits[2]), .q3(Last_4_bits[3]));  // open: shift, out, load, d0, d1, d2, d3
  xnor xnor_1 (xnor_1_out, Last_4_bits[3], Pattern_for_Detection[3]);
  xnor xnor_2 (xnor_2_out, Last_4_bits[2], Pattern_for_Detection[2]);
  xnor xnor_3 (xnor_3_out, Last_4_bits[1], Pattern_for_Detection[1]);
  xnor xnor_4 (xnor_4_out, Last_4_bits[0], Pattern_for_Detection[0]);
  and and_1 (Output, xnor_1_out, xnor_2_out, xnor_3_out, xnor_4_out);

  // Notes on the sheet:
  //   Comparision
endmodule
