// Logisim project p4.circ as structural Verilog: 1 circuit, main circuit main
module main (
  input  in_1,
  input  in_2,
  input  in_3,
  output out_4
);

  wire transistor_1_out, transistor_2_out, transistor_5_out;

  Transistor #(.\type ("n")) transistor_1 (.in(1'b1), .out(transistor_1_out), .gate(in_1));
  Transistor #(.\type ("n")) transistor_2 (.in(transistor_1_out), .out(transistor_2_out), .gate(in_2));
  Transistor transistor_3 (.in(1'b0), .out(transistor_2_out), .gate(in_1));
  Transistor transistor_4 (.in(1'b0), .out(transistor_2_out), .gate(in_2));
  Transistor #(.\type ("n")) transistor_5 (.in(1'b1), .out(transistor_5_out), .gate(transistor_2_out));
  Transistor #(.\type ("n")) transistor_6 (.in(transistor_5_out), .out(out_4), .gate(in_3));
  Transistor transistor_7 (.in(1'b0), .out(out_4), .gate(transistor_2_out));
  Transistor transistor_8 (.in(1'b0), .out(out_4), .gate(in_3));
endmodule
