// Logisim project p5.circ as structural Verilog: 1 circuit, main circuit main
module main (
  input  in_1,
  input  in_2,
  input  in_3,
  input  in_4,
  output out_5
);

  wire transistor_1_out, transistor_2_out, transistor_5_out, transistor_8_out, transistor_11_out;

  Transistor #(.\type ("n")) transistor_1 (.in(1'b1), .out(transistor_1_out), .gate(in_1));
  Transistor #(.\type ("n")) transistor_2 (.in(1'b1), .out(transistor_2_out), .gate(in_3));
  Transistor #(.\type ("n")) transistor_3 (.in(1'b1), .out(transistor_1_out), .gate(in_2));
  Transistor transistor_4 (.in(transistor_5_out), .out(transistor_1_out), .gate(in_1));
  Transistor transistor_5 (.in(1'b0), .out(transistor_5_out), .gate(in_2));
  Transistor #(.\type ("n")) transistor_6 (.in(1'b1), .out(transistor_2_out), .gate(in_4));
  Transistor transistor_7 (.in(transistor_8_out), .out(transistor_2_out), .gate(in_3));
  Transistor transistor_8 (.in(1'b0), .out(transistor_8_out), .gate(in_4));
  Transistor #(.\type ("n")) transistor_9 (.in(1'b1), .out(out_5), .gate(transistor_1_out));
  Transistor transistor_10 (.in(transistor_11_out), .out(out_5), .gate(transistor_1_out));
  Transistor transistor_11 (.in(1'b0), .out(transistor_11_out), .gate(transistor_2_out));
  Transistor #(.\type ("n")) transistor_12 (.in(1'b1), .out(out_5), .gate(transistor_2_out));
endmodule
