// Logisim project p6.circ as structural Verilog: 1 circuit, main circuit main
module main (
  input  in_1,
  input  in_2,
  output out_3
);

  wire transistor_1_out, transistor_2_out, transistor_3_out, transistor_6_out, transistor_12_out;

  Transistor transistor_1 (.in(1'b0), .out(transistor_1_out), .gate(in_1));
  Transistor transistor_2 (.in(1'b1), .out(transistor_2_out), .gate(in_1));
  Transistor transistor_3 (.in(transistor_2_out), .out(transistor_3_out), .gate(in_2));
  Transistor #(.\type ("n")) transistor_4 (.in(1'b0), .out(transistor_3_out), .gate(in_2));
  Transistor #(.\type ("n")) transistor_5 (.in(1'b0), .out(transistor_3_out), .gate(in_1));
  Transistor #(.\type ("n")) transistor_6 (.in(1'b1), .out(transistor_6_out), .gate(in_1));
  Transistor #(.\type ("n")) transistor_7 (.in(transistor_6_out), .out(transistor_1_out), .gate(in_2));
  Transistor transistor_8 (.in(1'b0), .out(transistor_1_out), .gate(in_2));
  Transistor #(.\type ("n")) transistor_9 (.in(1'b1), .out(out_3), .gate(transistor_1_out));
  Transistor #(.\type ("n")) transistor_10 (.in(1'b1), .out(out_3), .gate(transistor_3_out));
  Transistor transistor_11 (.in(transistor_12_out), .out(out_3), .gate(transistor_1_out));
  Transistor transistor_12 (.in(1'b0), .out(transistor_12_out), .gate(transistor_3_out));
endmodule
