// Logisim project L10Q1_D.circ as structural Verilog: 1 circuit, main circuit main
module main (
  input  C0,
  input  C1,
  input  Clear
);

  wire and_1_out, and_2_out, Clock_out, not_1_out, or_1_out, Q0, Q1, xor_1_out, xor_2_out, xor_3_out,
       xor_4_out;

  Clock Clock (.out(Clock_out));
  xor xor_1 (xor_1_out, Q0, xor_2_out);
  xor xor_2 (xor_2_out, C0, C1);
  D_Flip_Flop d_ff_1 (.clk(Clock_out), .D(xor_1_out), .Q(Q0), .reset(Clear));  // open: Qn, preset, en
  xor xor_3 (xor_3_out, C0, Q1);
  not not_1 (not_1_out, Q0);
  xor xor_4 (xor_4_out, Q1, C1);
  LED u_Q1 (.in(Q1));
  LED u_Q0 (.in(Q0));
  and and_1 (and_1_out, xor_3_out, not_1_out);
  or or_1 (or_1_out, and_1_out, and_2_out);
  and and_2 (and_2_out, Q0, xor_4_out);
  Hex_Digit_Display hex_digit_display_1 (.value({2'b00, Q1, Q0}));  // open: dp
  D_Flip_Flop d_ff_2 (.clk(Clock_out), .D(or_1_out), .Q(Q1), .reset(Clear));  // open: Qn, preset, en
endmodule
