// Logisim project L10Q1_JK.circ as structural Verilog: 1 circuit, main circuit main
module main (
  input  C0,
  input  C1,
  input  Clear
);

  wire and_1_out, and_2_out, Clock_out, not_1_out, or_1_out, Q0, xor_1_out;
  wire [1:1] j_k_ff_2_q;

  Clock Clock (.out(Clock_out));
  xor xor_1 (xor_1_out, C0, C1);
  and and_1 (and_1_out, Q0, C1);
  and and_2 (and_2_out, C0, not_1_out);
  not not_1 (not_1_out, Q0);
  J_K_Flip_Flop j_k_ff_1 (
    .J(xor_1_out), .clk(Clock_out), .K(xor_1_out), .Q(Q0), .reset(Clear));  // open: Qn, preset, en
  or or_1 (or_1_out, and_1_out, and_2_out);
  J_K_Flip_Flop j_k_ff_2 (
    .J(or_1_out), .clk(Clock_out), .K(or_1_out), .Q(j_k_ff_2_q[1]), .reset(Clear));  // open: Qn, preset, en
  LED Q1 (.in(j_k_ff_2_q[1]));
  LED u_Q0 (.in(Q0));
  Hex_Digit_Display hex_digit_display_1 (.value({2'b00, j_k_ff_2_q[1], Q0}));  // open: dp
endmodule
