// Logisim project L10Q1_SR.circ as structural Verilog: 1 circuit, main circuit main
module main (
  input  C0,
  input  C1,
  input  Clear
);

  wire and_1_out, and_2_out, and_3_out, and_4_out, and_5_out, and_6_out, Clock_out, not_1_out, not_2_out,
       not_3_out, or_1_out, Q0, Q1, xor_1_out;

  Clock Clock (.out(Clock_out));
  xor xor_1 (xor_1_out, C0, C1);
  not not_1 (not_1_out, Q0);
  not not_2 (not_2_out, Q0);
  and and_1 (and_1_out, not_2_out, xor_1_out);
  and and_2 (and_2_out, xor_1_out, Q0);
  and and_3 (and_3_out, C0, not_1_out);
  or or_1 (or_1_out, and_3_out, and_4_out);
  and and_4 (and_4_out, Q0, C1);
  S_R_Flip_Flop s_r_ff_1 (
    .S(and_1_out), .clk(Clock_out), .R(and_2_out), .Q(Q0), .reset(Clear));  // open: Qn, preset, en
  not not_3 (not_3_out, Q1);
  and and_5 (and_5_out, not_3_out, or_1_out);
  and and_6 (and_6_out, or_1_out, Q1);
  S_R_Flip_Flop s_r_ff_2 (
    .S(and_5_out), .clk(Clock_out), .R(and_6_out), .Q(Q1), .reset(Clear));  // open: Qn, preset, en
  LED u_Q1 (.in(Q1));
  Hex_Digit_Display hex_digit_display_1 (.value({2'b00, Q1, Q0}));  // open: dp
  LED u_Q0 (.in(Q0));
endmodule
