// Logisim project L10Q1_T.circ as structural Verilog: 1 circuit, main circuit main
module main (
  input  C0,
  input  C1,
  input  Clear
);

  wire and_1_out, and_2_out, Clock_out, not_1_out, or_1_out, Q0, Q1, xor_1_out;

  Clock Clock (.out(Clock_out));
  xor xor_1 (xor_1_out, C0, C1);
  and and_1 (and_1_out, Q0, C1);
  and and_2 (and_2_out, C0, not_1_out);
  not not_1 (not_1_out, Q0);
  T_Flip_Flop t_ff_1 (.clk(Clock_out), .T(xor_1_out), .Q(Q0), .reset(Clear));  // open: Qn, preset, en
  or or_1 (or_1_out, and_1_out, and_2_out);
  T_Flip_Flop t_ff_2 (.clk(Clock_out), .T(or_1_out), .Q(Q1), .reset(Clear));  // open: Qn, preset, en
  LED u_Q0 (.in(Q0));
  LED u_Q1 (.in(Q1));
  Hex_Digit_Display hex_digit_display_1 (.value({2'b00, Q1, Q0}));  // open: dp
endmodule
