// Logisim project Q2.circ as structural Verilog: 1 circuit, main circuit 8 bit adder
module _8_bit_adder (
  input  [7:0] A,
  input  in_2,
  input  in_3,
  input  [7:0] B,
  input  in_5,
  output [8:0] Y
);

  wire adder_1_cout, adder_1_out, Clock, Shift_Register_A_out, Shift_Register_B_out;

  Clock clock_1 (.out(Clock));
  Shift_Register Shift_Register_A (
    .shift(in_3), .clk(Clock), .out(Shift_Register_A_out), .load(in_2), .clr(in_5), .d0(A[7]), .d1(A[6]),
    .d2(A[5]), .d3(A[4]), .d4(A[3]), .d5(A[2]), .d6(A[1]), .d7(A[0]));  // open: in, q0, q1, q2, q3, q4, q5, q6, q7
  Shift_Register Shift_Register_B (
    .shift(in_3), .clk(Clock), .out(Shift_Register_B_out), .load(in_2), .clr(in_5), .d0(B[7]), .d1(B[6]),
    .d2(B[5]), .d3(B[4]), .d4(B[3]), .d5(B[2]), .d6(B[1]), .d7(B[0]));  // open: in, q0, q1, q2, q3, q4, q5, q6, q7
  D_Flip_Flop Carry (.clk(Clock), .D(adder_1_cout), .Q(Y[8]));  // open: Qn, preset, en, reset
  Adder #(.width(1)) adder_1 (
    .a(Shift_Register_A_out), .b(Shift_Register_B_out), .out(adder_1_out), .cin(Y[8]), .cout(adder_1_cout));
  Shift_Register Output_Shift_Register (
    .in(adder_1_out), .clk(Clock), .clr(in_5), .q0(Y[7]), .q1(Y[6]), .q2(Y[5]), .q3(Y[4]), .q4(Y[3]),
    .q5(Y[2]), .q6(Y[1]), .q7(Y[0]));  // open: shift, out, load, d0, d1, d2, d3, d4, d5, d6, d7

  // Other names for the same wires on the sheet: Load = in_2; Reset = in_5; Shift = in_3

  // Notes on the sheet:
  //   Carry Out
endmodule
