// Logisim project Q3.circ as structural Verilog: 3 circuits, main circuit 4-bit counter block diagram
module _4_bit_counter_block_diagram (
  input  Count,
  input  Clear
);

  wire Clock_out;
  wire [3:0] n4_bit_counter_1_q0;

  Clock Clock (.out(Clock_out));
  _4_bit_counter u_4_bit_counter_1 (
    .Clock(Clock_out), .Count(Count), .Clear(Clear), .q3(n4_bit_counter_1_q0[3]),
    .q2(n4_bit_counter_1_q0[2]), .q1(n4_bit_counter_1_q0[1]), .q0(n4_bit_counter_1_q0[0]));
  LED led_1 (.in(n4_bit_counter_1_q0[2]));
  LED led_2 (.in(n4_bit_counter_1_q0[1]));
  LED led_3 (.in(n4_bit_counter_1_q0[3]));
  Hex_Digit_Display hex_digit_display_1 (.value(n4_bit_counter_1_q0));  // open: dp
  LED led_4 (.in(n4_bit_counter_1_q0[0]));
endmodule

module _4_bit_counter (
  input  Clock,
  input  Count,
  input  Clear,
  output q3,
  output q2,
  output q1,
  output q0
);

  wire and_1_out;

  _2_bit_counter u_2_bit_counter_1 (.Clock(Clock), .Count(Count), .Clear(Clear), .q0(q0), .q1(q1));
  _2_bit_counter u_2_bit_counter_2 (.Clock(Clock), .Count(and_1_out), .Clear(Clear), .q0(q2), .q1(q3));
  and and_1 (and_1_out, q0, q1);
  Hex_Digit_Display hex_digit_display_1 (.value({q3, q2, q1, q0}));  // open: dp
endmodule

module _2_bit_counter (
  input  Clock,
  input  Count,
  input  Clear,
  output q0,
  output q1
);

  wire and_1_out;

  T_Flip_Flop t_ff_1 (.clk(Clock), .T(Count), .Q(q0), .reset(Clear));  // open: Qn, preset, en
  and and_1 (and_1_out, q0, Count);
  T_Flip_Flop t_ff_2 (.clk(Clock), .T(and_1_out), .Q(q1), .reset(Clear));  // open: Qn, preset, en
endmodule
