// Logisim project L11Q2_J-K-mealy.circ as structural Verilog: 1 circuit, main circuit main
module main (
  input  in_1,
  output Output
);

  wire and_1_out, Clock, nand_1_out, S0, S1, xor_1_out;

  Clock clock_1 (.out(Clock));
  xor xor_1 (xor_1_out, S1, in_1);
  nand nand_1 (nand_1_out, S1, in_1);
  and and_1 (and_1_out, in_1, S0);
  J_K_Flip_Flop j_k_ff_1 (.J(xor_1_out), .clk(Clock), .K(nand_1_out), .Q(S0));  // open: Qn, preset, en, reset
  J_K_Flip_Flop j_k_ff_2 (.J(and_1_out), .clk(Clock), .K(S0), .Q(S1));  // open: Qn, preset, en, reset
  and and_2 (Output, S0, in_1, S1);

  // Other names for the same wires on the sheet: A = in_1

  // Notes on the sheet:
  //   J0
  //   K0
  //   J1
  //   K1
endmodule
