// Logisim project L11Q2_J-K-moore.circ as structural Verilog: 1 circuit, main circuit main
module main (
  input  in_1,
  output Output
);

  wire and_1_out, and_2_out, and_3_out, Clock, or_1_out, S0, S1, xor_1_out, xor_2_out;

  Clock clock_1 (.out(Clock));
  xor xor_1 (xor_1_out, S1, in_1);
  xor xor_2 (xor_2_out, Output, S0);
  and and_1 (and_1_out, xor_2_out, in_1);
  or or_1 (or_1_out, Output, S0);
  and and_2 (and_2_out, in_1, S1, S0);
  and and_3 (and_3_out, ~Output, xor_1_out);  // AND_Gate
  J_K_Flip_Flop j_k_ff_1 (.J(and_3_out), .clk(Clock), .K(1'b1), .Q(S0));  // open: Qn, preset, en, reset
  J_K_Flip_Flop j_k_ff_2 (.J(and_1_out), .clk(Clock), .K(or_1_out), .Q(S1));  // open: Qn, preset, en, reset
  J_K_Flip_Flop j_k_ff_3 (.J(and_2_out), .clk(Clock), .K(1'b1), .Q(Output));  // open: Qn, preset, en, reset

  // Other names for the same wires on the sheet: A = in_1; S2 = Output

  // Notes on the sheet:
  //   J0
  //   K0
  //   J1
  //   K1
  //   J2
  //   K2
endmodule
