// Logisim project L11Q2_T-mealy.circ as structural Verilog: 1 circuit, main circuit main
module main (
  input  in_1,
  output Output
);

  wire and_1_out, and_2_out, and_3_out, Clock, or_1_out, or_2_out, S0, S1, xor_1_out;

  Clock clock_1 (.out(Clock));
  xor xor_1 (xor_1_out, S1, in_1);
  and and_1 (and_1_out, ~in_1, S0);  // AND_Gate
  and and_2 (and_2_out, S1, S0);
  and and_3 (and_3_out, S0, in_1);
  or or_1 (or_1_out, xor_1_out, and_1_out);
  or or_2 (or_2_out, and_2_out, and_3_out);
  T_Flip_Flop t_ff_1 (.clk(Clock), .T(or_1_out), .Q(S0));  // open: Qn, preset, reset, en
  T_Flip_Flop t_ff_2 (.clk(Clock), .T(or_2_out), .Q(S1));  // open: Qn, preset, reset, en
  and and_4 (Output, S0, in_1, S1);

  // Other names for the same wires on the sheet: A = in_1

  // Notes on the sheet:
  //   T0
  //   T1
endmodule
