// Logisim project L11Q2_T-moore.circ as structural Verilog: 1 circuit, main circuit main
module main (
  input  in_1,
  output Output
);

  wire and_1_out, and_2_out, and_3_out, and_4_out, Clock, or_1_out, or_2_out, or_3_out, S0, S1, xor_1_out,
       xor_2_out;

  Clock clock_1 (.out(Clock));
  or or_1 (or_1_out, Output, S0);
  xor xor_1 (xor_1_out, Output, S0);
  and and_1 (and_1_out, ~Output, xor_2_out);  // AND_Gate
  xor xor_2 (xor_2_out, S1, in_1);
  and and_2 (and_2_out, S1, or_1_out);
  and and_3 (and_3_out, in_1, xor_1_out);
  or or_2 (or_2_out, Output, and_4_out);
  and and_4 (and_4_out, S1, S0, in_1);
  or or_3 (or_3_out, and_2_out, and_3_out);
  T_Flip_Flop t_ff_1 (.clk(Clock), .T(and_1_out), .Q(S0));  // open: Qn, preset, reset, en
  T_Flip_Flop t_ff_2 (.clk(Clock), .T(or_3_out), .Q(S1));  // open: Qn, preset, reset, en
  T_Flip_Flop t_ff_3 (.clk(Clock), .T(or_2_out), .Q(Output));  // open: Qn, preset, reset, en

  // Other names for the same wires on the sheet: A = in_1; S2 = Output

  // Notes on the sheet:
  //   T0
  //   T1
  //   T2
endmodule
