// Logisim project Q3.circ as structural Verilog: 1 circuit, main circuit main
module main (
  input  [7:0] New_Value,
  input  Hist_En,
  input  Sum_En,
  input  Load,
  input  Shift,
  input  Reset_sum,
  input  Reset_hist,
  output [7:0] Average
);

  wire Clock_out;
  wire [7:0] adder_1_out, adder_2_out, adder_3_out, Register_1_q, Register_2_q, Register_3_q, Register_4_q,
       Sum_Register_q;

  Clock Clock (.out(Clock_out));
  Register Register_1 (.D(New_Value), .en(Hist_En), .Q(Register_1_q), .clk(Clock_out), .clr(Reset_hist));
  Register Register_2 (.D(Register_1_q), .en(Hist_En), .Q(Register_2_q), .clk(Clock_out), .clr(Reset_hist));
  Register Register_3 (.D(Register_2_q), .en(Hist_En), .Q(Register_3_q), .clk(Clock_out), .clr(Reset_hist));
  Adder adder_1 (.a(Register_2_q), .b(Register_1_q), .out(adder_1_out));  // open: cin, cout
  Register Register_4 (.D(Register_3_q), .en(Hist_En), .Q(Register_4_q), .clk(Clock_out), .clr(Reset_hist));
  Adder adder_2 (.a(Register_3_q), .b(adder_1_out), .out(adder_2_out));  // open: cin, cout
  Register Sum_Register (.D(adder_3_out), .en(Sum_En), .Q(Sum_Register_q), .clk(Clock_out), .clr(Reset_sum));
  Adder adder_3 (.a(Register_4_q), .b(adder_2_out), .out(adder_3_out));  // open: cin, cout
  Shift_Register shift_register_1 (
    .shift(Shift), .in(1'b0), .clk(Clock_out), .load(Load), .clr(Reset_sum), .d0(Sum_Register_q[7]),
    .q0(Average[7]), .d1(Sum_Register_q[6]), .q1(Average[6]), .d2(Sum_Register_q[5]), .q2(Average[5]),
    .d3(Sum_Register_q[4]), .q3(Average[4]), .d4(Sum_Register_q[3]), .q4(Average[3]), .d5(Sum_Register_q[2]),
    .q5(Average[2]), .d6(Sum_Register_q[1]), .q6(Average[1]), .d7(Sum_Register_q[0]), .q7(Average[0]));  // open: out

  // Notes on the sheet:
  //   History of Temperatures
  //   Shift Register
  //    for Division
endmodule
