// Logisim project p3(c) - Logisim.circ as structural Verilog: 2 circuits, main circuit ALU
module p3_c (
  input  [7:0] Input,
  input  Clear,
  input  Reset,
  output [7:0] Output
);

  wire and_1_out, and_2_out, and_3_out, and_4_out, and_5_out, and_6_out, and_7_out, Clock, decoder_1_out1,
       decoder_1_out2, decoder_1_out3, decoder_1_out4, decoder_1_out5, decoder_1_out6, decoder_1_out7;
  wire [1:0] multiplexer_1_out, State;
  wire [2:0] SELD;
  wire [7:0] multiplexer_3_out, multiplexer_4_out, R1_q, R2_q, R3_q, R4_q, R5_q, R6_q, R7_q;

  Clock u_Clock (.out(Clock));
  Multiplexer #(.select(2), .width(2), .enable("false")) multiplexer_1 (
    .in0(2'b01), .in1(2'b10), .in2(2'b00), .in3(2'b00), .out(multiplexer_1_out), .sel(State));
  Register #(.width(2)) u_State (.D(multiplexer_1_out), .Q(State), .clk(Clock), .clr(Reset));  // open: en
  Multiplexer #(.select(2), .width(3), .enable("false")) multiplexer_2 (
    .in0(3'b000), .in1(3'b000), .in2(3'b111), .in3(3'b000), .out(SELD), .sel(State));
  Decoder #(.select(3), .enable("false")) decoder_1 (
    .out1(decoder_1_out1), .out2(decoder_1_out2), .out3(decoder_1_out3), .out4(decoder_1_out4),
    .out5(decoder_1_out5), .out6(decoder_1_out6), .out7(decoder_1_out7), .sel(SELD));  // open: out0
  and and_1 (and_1_out, State[1], ~State[0], decoder_1_out1);  // AND_Gate
  and and_2 (and_2_out, State[1], ~State[0], decoder_1_out2);  // AND_Gate
  and and_3 (and_3_out, State[1], ~State[0], decoder_1_out3);  // AND_Gate
  and and_4 (and_4_out, State[1], ~State[0], decoder_1_out4);  // AND_Gate
  and and_5 (and_5_out, State[1], ~State[0], decoder_1_out5);  // AND_Gate
  and and_6 (and_6_out, State[1], ~State[0], decoder_1_out6);  // AND_Gate
  and and_7 (and_7_out, State[1], ~State[0], decoder_1_out7);  // AND_Gate
  Register R1 (.D(Output), .en(and_1_out), .Q(R1_q), .clk(Clock), .clr(Clear));
  Register R2 (.D(Output), .en(and_2_out), .Q(R2_q), .clk(Clock), .clr(Clear));
  Register R3 (.D(Output), .en(and_3_out), .Q(R3_q), .clk(Clock), .clr(Clear));
  Register R4 (.D(Output), .en(and_4_out), .Q(R4_q), .clk(Clock), .clr(Clear));
  Register R5 (.D(Output), .en(and_5_out), .Q(R5_q), .clk(Clock), .clr(Clear));
  Register R6 (.D(Output), .en(and_6_out), .Q(R6_q), .clk(Clock), .clr(Clear));
  Register R7 (.D(Output), .en(and_7_out), .Q(R7_q), .clk(Clock), .clr(Clear));
  Multiplexer #(.select(3), .width(8), .enable("false")) multiplexer_3 (
    .in0(Input), .in1(R1_q), .in2(R2_q), .in3(R3_q), .in4(R4_q), .in5(R5_q), .in6(R6_q), .in7(R7_q),
    .out(multiplexer_3_out), .sel(3'b000));
  Multiplexer #(.select(3), .width(8), .enable("false")) multiplexer_4 (
    .in0(Input), .in1(R1_q), .in2(R2_q), .in3(R3_q), .in4(R4_q), .in5(R5_q), .in6(R6_q), .in7(R7_q),
    .out(multiplexer_4_out), .sel(3'b001));
  ALU ALU (.A(multiplexer_3_out), .B(multiplexer_4_out), .in_3({5{1'b0}}), .out_4(Output));

  // Notes on the sheet:
  //   State Transition
  //   Ans 3c) FSM to add 2 numbers from Registers R1-R7 of given block
  //   00000 for
  //   Addition
endmodule

module ALU (
  input  [7:0] A,
  input  [7:0] B,
  input  [4:0] in_3,
  output [7:0] out_4
);

  wire comparator_1_eq, comparator_1_gt, comparator_1_lt;
  wire [7:0] adder_1_out, adder_2_out, adder_3_out, and_1_out, and_2_out, and_3_out, bit_extender_1_out,
       bit_extender_2_out, bit_extender_3_out, divider_1_out, multiplier_1_out, nand_1_out, negator_1_out,
       negator_2_out, nor_1_out, not_1_out, not_2_out, or_1_out, or_2_out, or_3_out, shifter_1_out,
       shifter_2_out, shifter_3_out, shifter_4_out, subtractor_1_out, xnor_1_out, xor_1_out, xor_2_out,
       xor_3_out;

  Adder adder_1 (.a(A), .b(B), .out(adder_1_out), .cin(1'b0));  // open: cout
  Subtractor subtractor_1 (.a(A), .b(B), .out(subtractor_1_out), .bin(1'b0));  // open: bout
  assign and_1_out = A & B;  // AND_Gate and_1, 8 bits wide
  assign or_1_out = A | B;  // OR_Gate or_1, 8 bits wide
  assign nand_1_out = ~(A & B);  // NAND_Gate nand_1, 8 bits wide
  assign nor_1_out = ~(A | B);  // NOR_Gate nor_1, 8 bits wide
  assign xor_1_out = A ^ B;  // XOR_Gate xor_1, 8 bits wide
  assign xnor_1_out = ~(A ^ B);  // XNOR_Gate xnor_1, 8 bits wide
  Comparator #(.mode("unsigned")) comparator_1 (
    .a(A), .b(B), .gt(comparator_1_gt), .eq(comparator_1_eq), .lt(comparator_1_lt));
  Multiplier multiplier_1 (.a(A), .b(B), .out(multiplier_1_out), .cin({8{1'b0}}));  // open: cout
  Divider divider_1 (.a(A), .b(B), .out(divider_1_out), .upper({8{1'b0}}));  // open: rem
  Negator negator_1 (.in(A), .out(negator_1_out));
  Negator negator_2 (.in(B), .out(negator_2_out));
  Shifter shifter_1 (.in(A), .\dist (3'b001), .out(shifter_1_out));
  Shifter shifter_2 (.in(B), .\dist (3'b001), .out(shifter_2_out));
  assign not_1_out = ~A;  // NOT_Gate not_1, 8 bits wide
  assign not_2_out = ~B;  // NOT_Gate not_2, 8 bits wide
  assign and_2_out = ~A & B;  // AND_Gate and_2, 8 bits wide
  assign and_3_out = A & ~B;  // AND_Gate and_3, 8 bits wide
  assign or_2_out = ~A | B;  // OR_Gate or_2, 8 bits wide
  assign or_3_out = A | ~B;  // OR_Gate or_3, 8 bits wide
  assign xor_2_out = A ^ {8{1'b1}};  // XOR_Gate xor_2, 8 bits wide
  assign xor_3_out = B ^ {8{1'b1}};  // XOR_Gate xor_3, 8 bits wide
  assign bit_extender_1_out = {{7{1'b0}}, comparator_1_gt};  // Bit_Extender bit_extender_1
  assign bit_extender_2_out = {{7{1'b0}}, comparator_1_eq};  // Bit_Extender bit_extender_2
  assign bit_extender_3_out = {{7{1'b0}}, comparator_1_lt};  // Bit_Extender bit_extender_3
  Shifter shifter_3 (.in(B), .\dist (3'b001), .out(shifter_3_out));
  Shifter shifter_4 (.in(B), .\dist (3'b001), .out(shifter_4_out));
  Adder adder_2 (.a(xor_3_out), .b({8{1'b0}}), .out(adder_2_out), .cin(1'b1));  // open: cout
  Adder adder_3 (.a(xor_2_out), .b({8{1'b0}}), .out(adder_3_out), .cin(1'b1));  // open: cout
  Multiplexer #(.select(5), .width(8), .enable("false")) multiplexer_1 (
    .in0(adder_1_out), .in1(subtractor_1_out), .in2(and_1_out), .in3(or_1_out), .in4(nand_1_out),
    .in5(nor_1_out), .in6(xor_1_out), .in7(xnor_1_out), .in8(bit_extender_2_out), .in9(bit_extender_1_out),
    .in10(bit_extender_3_out), .in11(multiplier_1_out), .in12(divider_1_out), .in13(negator_1_out),
    .in14(negator_2_out), .in15(shifter_1_out), .in16(shifter_2_out), .in17(shifter_3_out),
    .in18(shifter_4_out), .in19(not_1_out), .in20(not_2_out), .in21(and_2_out), .in22(and_3_out),
    .in23(or_2_out), .in24(or_3_out), .in25(A), .in26(B), .in27(xor_2_out), .in28(xor_3_out),
    .in29(adder_3_out), .in30(adder_2_out), .in31({A[0], A[1], A[2], A[3], A[4], A[5], A[6], A[7]}),
    .out(out_4), .sel(in_3));
endmodule
