// Logisim project p1.circ as structural Verilog: 1 circuit, main circuit main
module main (
  input  in_1,
  input  in_2,
  input  in_3,
  input  in_4,
  output out_5
);

  wire transistor_1_out, transistor_2_out, transistor_4_out;

  Transistor transistor_1 (.in(1'b1), .out(transistor_1_out), .gate(in_1));
  Transistor transistor_2 (.in(transistor_1_out), .out(transistor_2_out), .gate(in_2));
  Transistor transistor_3 (.in(transistor_4_out), .out(out_5), .gate(in_4));
  Transistor transistor_4 (.in(transistor_2_out), .out(transistor_4_out), .gate(in_3));
endmodule
