// Logisim project p2.circ as structural Verilog: 1 circuit, main circuit main
module main (
  input  in_1,
  input  in_2,
  input  in_3,
  input  in_4,
  input  in_5,
  input  in_6,
  input  in_7,
  input  in_8,
  input  in_9,
  input  in_10,
  input  in_11,
  input  in_12,
  input  in_13,
  input  in_14,
  input  in_15,
  input  in_16,
  input  in_17,
  input  in_18,
  input  in_19,
  input  in_20,
  output out_21,
  output out_22,
  output out_23,
  output out_24
);

  wire transistor_2_out, transistor_3_out, transistor_4_out, transistor_5_out, transistor_6_out,
       transistor_7_out, transistor_8_out, transistor_9_out, transistor_10_out, transistor_12_out,
       transistor_16_out, transistor_21_out;

  Pull_Resistor #(.pull(1)) pull_resistor_1 (.node(out_21));
  Transistor #(.\type ("n")) transistor_1 (.in(transistor_2_out), .out(out_21), .gate(in_1));
  Transistor #(.\type ("n")) transistor_2 (.in(transistor_3_out), .out(transistor_2_out), .gate(in_2));
  Transistor #(.\type ("n")) transistor_3 (.in(transistor_4_out), .out(transistor_3_out), .gate(in_8));
  Transistor #(.\type ("n")) transistor_4 (.in(transistor_5_out), .out(transistor_4_out), .gate(in_9));
  Transistor #(.\type ("n")) transistor_5 (.in(1'b0), .out(transistor_5_out), .gate(in_10));
  Transistor #(.\type ("n")) transistor_6 (.in(transistor_7_out), .out(transistor_6_out), .gate(in_16));
  Pull_Resistor #(.pull(1)) pull_resistor_2 (.node(transistor_6_out));
  Transistor #(.\type ("n")) transistor_7 (.in(transistor_8_out), .out(transistor_7_out), .gate(in_17));
  Transistor #(.\type ("n")) transistor_8 (.in(transistor_9_out), .out(transistor_8_out), .gate(in_18));
  Transistor #(.\type ("n")) transistor_9 (.in(transistor_10_out), .out(transistor_9_out), .gate(in_19));
  Transistor #(.\type ("n")) transistor_10 (.in(1'b0), .out(transistor_10_out), .gate(in_20));
  Pull_Resistor #(.pull(1)) pull_resistor_3 (.node(out_24));
  Transistor #(.\type ("n")) transistor_11 (.in(transistor_12_out), .out(out_24), .gate(transistor_6_out));
  Transistor #(.\type ("n")) transistor_12 (.in(1'b0), .out(transistor_12_out), .gate(transistor_6_out));
  Transistor #(.\type ("n")) transistor_13 (.in(1'b0), .out(out_22), .gate(in_3));
  Pull_Resistor #(.pull(1)) pull_resistor_4 (.node(out_22));
  Transistor #(.\type ("n")) transistor_14 (.in(1'b0), .out(out_22), .gate(in_4));
  Transistor #(.\type ("n")) transistor_15 (.in(1'b0), .out(out_22), .gate(in_5));
  Transistor #(.\type ("n")) transistor_16 (.in(1'b0), .out(transistor_16_out), .gate(in_11));
  Transistor #(.\type ("n")) transistor_17 (.in(1'b0), .out(out_22), .gate(in_6));
  Transistor #(.\type ("n")) transistor_18 (.in(1'b0), .out(out_22), .gate(in_7));
  Transistor #(.\type ("n")) transistor_19 (.in(1'b0), .out(transistor_16_out), .gate(in_12));
  Pull_Resistor #(.pull(1)) pull_resistor_5 (.node(out_23));
  Transistor #(.\type ("n")) transistor_20 (.in(transistor_21_out), .out(out_23), .gate(transistor_16_out));
  Transistor #(.\type ("n")) transistor_21 (.in(1'b0), .out(transistor_21_out), .gate(transistor_16_out));
  Pull_Resistor #(.pull(1)) pull_resistor_6 (.node(transistor_16_out));
  Transistor #(.\type ("n")) transistor_22 (.in(1'b0), .out(transistor_16_out), .gate(in_13));
  Transistor #(.\type ("n")) transistor_23 (.in(1'b0), .out(transistor_16_out), .gate(in_14));
  Transistor #(.\type ("n")) transistor_24 (.in(1'b0), .out(transistor_16_out), .gate(in_15));
endmodule
