// Logisim project p4.circ as structural Verilog
module main (
  input  in_1,
  input  in_2,
  input  in_3,
  input  in_4,
  input  in_5,
  output out_6
);

  wire transistor_1_out, transistor_2_out, transistor_3_out, transistor_4_out, transistor_9_out,
       transistor_12_out;

  Transistor transistor_1 (.in(1'b1), .out(transistor_1_out), .gate(in_1));
  Transistor transistor_2 (.in(transistor_1_out), .out(transistor_2_out), .gate(in_3));
  Transistor #(.\type ("n")) transistor_3 (.in(transistor_4_out), .out(transistor_3_out), .gate(in_1));
  Transistor #(.\type ("n")) transistor_4 (.in(1'b0), .out(transistor_4_out), .gate(in_2));
  Transistor transistor_5 (.in(1'b1), .out(transistor_1_out), .gate(in_2));
  Transistor transistor_6 (.in(transistor_1_out), .out(transistor_2_out), .gate(in_4));
  Transistor transistor_7 (.in(transistor_2_out), .out(transistor_3_out), .gate(in_5));
  Transistor #(.\type ("n")) transistor_8 (.in(transistor_9_out), .out(transistor_3_out), .gate(in_3));
  Transistor #(.\type ("n")) transistor_9 (.in(1'b0), .out(transistor_9_out), .gate(in_4));
  Transistor #(.\type ("n")) transistor_10 (.in(1'b0), .out(transistor_3_out), .gate(in_5));
  Transistor #(.\type ("n")) transistor_11 (.in(transistor_12_out), .out(out_6), .gate(transistor_3_out));
  Pull_Resistor #(.pull(1)) pull_resistor_1 (.node(out_6));
  Transistor #(.\type ("n")) transistor_12 (.in(1'b0), .out(transistor_12_out), .gate(transistor_3_out));

  // Other names for the same wires on the sheet: a = in_1; b = in_2; c = in_3; d = in_4; e = in_5
endmodule

module qwe (
  input  in_1,
  input  in_2,
  input  in_3,
  input  in_4,
  input  in_5,
  output out_6
);

  main main_1 (.in_1(in_1), .in_2(in_2), .in_3(in_5), .in_4(in_3), .in_5(in_4), .out_6(out_6));
endmodule

module abcde (
);

  wire undriven, undriven_2, undriven_3, undriven_4;

  qwe qwe_1 (.in_1(undriven_2), .in_2(undriven_3), .in_3(undriven_4), .in_4(undriven), .in_5(undriven));  // open: out_6
endmodule
