// Logisim project p6.circ as structural Verilog: 1 circuit, main circuit main
module main (
  input  in_1,
  input  in_2,
  input  in_3,
  input  in_4,
  output out_5,
  output out_6
);

  wire and_1_out, transistor_1_out, transistor_2_out, transistor_3_out, transistor_7_out, transistor_10_out;

  Transistor #(.\type ("n")) transistor_1 (.in(1'b0), .out(transistor_1_out), .gate(in_1));
  Transistor transistor_2 (.in(1'b1), .out(transistor_2_out), .gate(in_1));
  Transistor transistor_3 (.in(transistor_2_out), .out(transistor_3_out), .gate(in_3));
  Transistor transistor_4 (.in(transistor_2_out), .out(transistor_3_out), .gate(in_2));
  Transistor transistor_5 (.in(transistor_3_out), .out(transistor_1_out), .gate(in_4));
  Transistor #(.\type ("n")) transistor_6 (.in(transistor_7_out), .out(transistor_1_out), .gate(in_3));
  Transistor #(.\type ("n")) transistor_7 (.in(1'b0), .out(transistor_7_out), .gate(in_2));
  Transistor #(.\type ("n")) transistor_8 (.in(1'b0), .out(transistor_1_out), .gate(in_4));
  Transistor #(.\type ("n")) transistor_9 (.in(transistor_10_out), .out(out_6), .gate(transistor_1_out));
  Pull_Resistor #(.pull(1)) pull_resistor_1 (.node(out_6));
  Transistor #(.\type ("n")) transistor_10 (.in(1'b0), .out(transistor_10_out), .gate(transistor_1_out));
  and and_1 (and_1_out, 1'b1, in_3, 1'b1, in_2, 1'b1);
  or or_1 (out_5, in_1, 1'b0, 1'b0, and_1_out, in_4);
endmodule
