// Logisim project p7.circ as structural Verilog: 1 circuit, main circuit main
module main (
  input  in_1,
  input  in_2,
  input  in_3,
  input  in_4,
  input  in_5,
  input  in_6,
  output out_7,
  output out_8,
  output out_9
);

  wire transistor_5_out, transistor_6_out, transistor_7_out, transistor_8_out, transistor_9_out,
       transistor_16_out, transistor_17_out, transistor_18_out, transistor_19_out, transistor_20_out,
       transistor_23_out, transistor_28_out, transistor_29_out, transistor_30_out, transistor_31_out,
       transistor_32_out, transistor_38_out;

  Transistor transistor_1 (.in(1'b1), .out(out_7), .gate(in_1));
  Transistor transistor_2 (.in(1'b1), .out(out_7), .gate(in_2));
  Transistor transistor_3 (.in(1'b1), .out(out_7), .gate(in_3));
  Transistor #(.\type ("n")) transistor_4 (.in(transistor_5_out), .out(out_7), .gate(in_1));
  Transistor #(.\type ("n")) transistor_5 (.in(transistor_6_out), .out(transistor_5_out), .gate(in_2));
  Transistor #(.\type ("n")) transistor_6 (.in(transistor_7_out), .out(transistor_6_out), .gate(in_3));
  Transistor #(.\type ("n")) transistor_7 (.in(transistor_8_out), .out(transistor_7_out), .gate(in_4));
  Transistor #(.\type ("n")) transistor_8 (.in(transistor_9_out), .out(transistor_8_out), .gate(in_5));
  Transistor #(.\type ("n")) transistor_9 (.in(1'b0), .out(transistor_9_out), .gate(in_6));
  Transistor transistor_10 (.in(1'b1), .out(out_7), .gate(in_5));
  Transistor transistor_11 (.in(1'b1), .out(out_7), .gate(in_4));
  Transistor #(.\type ("n")) transistor_12 (.in(1'b0), .out(out_9), .gate(in_1));
  Transistor transistor_13 (.in(1'b1), .out(out_7), .gate(in_6));
  Transistor #(.\type ("n")) transistor_14 (.in(1'b0), .out(out_9), .gate(in_3));
  Transistor #(.\type ("n")) transistor_15 (.in(1'b0), .out(out_9), .gate(in_2));
  Transistor transistor_16 (.in(1'b1), .out(transistor_16_out), .gate(in_1));
  Transistor transistor_17 (.in(transistor_16_out), .out(transistor_17_out), .gate(in_2));
  Transistor transistor_18 (.in(transistor_17_out), .out(transistor_18_out), .gate(in_3));
  Transistor transistor_19 (.in(transistor_18_out), .out(transistor_19_out), .gate(in_4));
  Transistor transistor_20 (.in(transistor_19_out), .out(transistor_20_out), .gate(in_5));
  Transistor transistor_21 (.in(transistor_20_out), .out(out_9), .gate(in_6));
  Transistor #(.\type ("n")) transistor_22 (.in(1'b0), .out(out_9), .gate(in_4));
  Transistor transistor_23 (.in(1'b1), .out(transistor_23_out), .gate(in_1));
  Transistor transistor_24 (.in(1'b1), .out(transistor_23_out), .gate(in_2));
  Transistor #(.\type ("n")) transistor_25 (.in(1'b0), .out(out_9), .gate(in_5));
  Transistor transistor_26 (.in(1'b1), .out(transistor_23_out), .gate(in_3));
  Transistor #(.\type ("n")) transistor_27 (.in(transistor_28_out), .out(transistor_23_out), .gate(in_1));
  Transistor #(.\type ("n")) transistor_28 (.in(transistor_29_out), .out(transistor_28_out), .gate(in_2));
  Transistor #(.\type ("n")) transistor_29 (.in(transistor_30_out), .out(transistor_29_out), .gate(in_3));
  Transistor #(.\type ("n")) transistor_30 (.in(transistor_31_out), .out(transistor_30_out), .gate(in_4));
  Transistor #(.\type ("n")) transistor_31 (.in(transistor_32_out), .out(transistor_31_out), .gate(in_5));
  Transistor #(.\type ("n")) transistor_32 (.in(1'b0), .out(transistor_32_out), .gate(in_6));
  Transistor #(.\type ("n")) transistor_33 (.in(1'b0), .out(out_9), .gate(in_6));
  Transistor transistor_34 (.in(1'b1), .out(transistor_23_out), .gate(in_4));
  Transistor transistor_35 (.in(1'b1), .out(transistor_23_out), .gate(in_5));
  Transistor transistor_36 (.in(1'b1), .out(transistor_23_out), .gate(in_6));
  Transistor #(.\type ("n")) transistor_37 (.in(transistor_38_out), .out(out_8), .gate(transistor_23_out));
  Pull_Resistor #(.pull(1)) pull_resistor_1 (.node(out_8));
  Transistor #(.\type ("n")) transistor_38 (.in(1'b0), .out(transistor_38_out), .gate(transistor_23_out));

  // Other names for the same wires on the sheet: a = in_1; b = in_2; c = in_3; d = in_4; e = in_5; f = in_6
endmodule
