// Logisim project p10.circ as structural Verilog: 1 circuit, main circuit main
module main (
  input  a1,
  input  a0,
  input  b1,
  input  b0,
  output s0,
  output c,
  output s1
);

  wire a0_prime, a1_prime, and_1_out, and_2_out, and_3_out, and_4_out, and_5_out, and_6_out, and_7_out,
       and_8_out, and_9_out, and_10_out, and_11_out, b0_prime, b1_prime;

  not not_1 (a1_prime, a1);
  not not_2 (a0_prime, a0);
  not not_3 (b1_prime, b1);
  not not_4 (b0_prime, b0);
  and and_1 (and_1_out, a0_prime, b0);
  and and_2 (and_2_out, a0, b0_prime);
  and and_3 (and_3_out, a1_prime, a0_prime, b1);
  and and_4 (and_4_out, a1_prime, b1, b0);
  and and_5 (and_5_out, a1, a0_prime, b1_prime);
  and and_6 (and_6_out, a1, b0_prime, b1_prime);
  and and_7 (and_7_out, a1, a0, b1, b0);
  and and_8 (and_8_out, a1_prime, a0, b1_prime, b0);
  or or_1 (s0, and_1_out, and_2_out);
  or or_2 (s1, and_3_out, and_4_out, and_5_out, and_6_out, and_7_out, and_8_out);
  and and_9 (and_9_out, a0, b1, b0);
  and and_10 (and_10_out, a0, a1, b0);
  and and_11 (and_11_out, a1, b1);
  or or_3 (c, and_9_out, and_10_out, and_11_out);
endmodule
