// Logisim project p4.circ as structural Verilog: 1 circuit, main circuit main
module main (
  input  s0,
  input  s1,
  input  s2,
  input  s3,
  input  A,
  input  B,
  input  C,
  input  D,
  output x1,
  output x0,
  output out_11
);

  wire and_1_out, and_2_out, and_3_out, and_4_out, and_5_out, not_1_out, not_2_out, not_3_out, not_4_out;

  not not_1 (not_1_out, s0);
  not not_2 (not_2_out, s1);
  and and_1 (and_1_out, not_2_out, not_1_out, s2);
  or or_1 (x0, s1, s3);
  not not_3 (not_3_out, x1);
  not not_4 (not_4_out, x0);
  or or_2 (x1, and_1_out, s3);
  and and_2 (and_2_out, not_3_out, A, not_4_out);
  and and_3 (and_3_out, not_3_out, B, x0);
  and and_4 (and_4_out, x1, C, not_4_out);
  and and_5 (and_5_out, x1, D, x0);
  or or_3 (out_11, and_2_out, and_3_out, and_4_out, and_5_out);
endmodule
