// Logisim project p5.circ as structural Verilog: 2 circuits, main circuit main
module main (
  input  a3,
  input  b3,
  input  a2,
  input  b2,
  input  a1,
  input  in_6,
  input  b1,
  input  a0,
  input  b0,
  output d3,
  output d2,
  output d1,
  output d0
);

  _2x1_MUX u_2x1_mux_1 (.i0(a3), .i1(b3), .s0(in_6), .d(d3));
  _2x1_MUX u_2x1_mux_2 (.i0(a2), .i1(b2), .s0(in_6), .d(d2));
  _2x1_MUX u_2x1_mux_3 (.i0(a1), .i1(b1), .s0(in_6), .d(d1));
  _2x1_MUX u_2x1_mux_4 (.i0(a0), .i1(b0), .s0(in_6), .d(d0));
endmodule

module _2x1_MUX (
  input  i0,
  input  i1,
  input  s0,
  output d
);

  wire and_1_out, and_2_out, not_1_out;

  not not_1 (not_1_out, s0);
  and and_1 (and_1_out, i0, not_1_out);
  and and_2 (and_2_out, i1, s0);
  or or_1 (d, and_1_out, and_2_out);
endmodule
