// Logisim project p6.circ as structural Verilog: 2 circuits, main circuit main
module main (
  input  b3,
  input  a3,
  input  c3,
  input  d3,
  input  s1,
  input  b2,
  input  a2,
  input  s0,
  input  c2,
  input  d2,
  input  b1,
  input  a1,
  input  c1,
  input  d1,
  input  b0,
  input  a0,
  input  c0,
  input  d0,
  output out_19,
  output out_20,
  output out_21,
  output out_22
);

  _4x1_MUX u_4x1_mux_1 (.i0(a3), .i1(b3), .i2(c3), .i3(d3), .s1(s1), .s0(s0), .d(out_19));
  _4x1_MUX u_4x1_mux_2 (.i0(a2), .i1(b2), .i2(c2), .i3(d2), .s1(s1), .s0(s0), .d(out_20));
  _4x1_MUX u_4x1_mux_3 (.i0(a1), .i1(b1), .i2(c1), .i3(d1), .s1(s1), .s0(s0), .d(out_21));
  _4x1_MUX u_4x1_mux_4 (.i0(a0), .i1(b0), .i2(c0), .i3(d0), .s1(s1), .s0(s0), .d(out_22));
endmodule

module _4x1_MUX (
  input  i0,
  input  i1,
  input  i2,
  input  i3,
  input  s1,
  input  s0,
  output d
);

  wire and_1_out, and_2_out, and_3_out, and_4_out, not_1_out, not_2_out;

  not not_1 (not_1_out, s1);
  not not_2 (not_2_out, s0);
  and and_1 (and_1_out, i0, not_1_out, not_2_out);
  and and_2 (and_2_out, i1, s0, not_1_out);
  and and_3 (and_3_out, i2, not_2_out, s1);
  and and_4 (and_4_out, i3, s1, s0);
  or or_1 (d, and_1_out, and_2_out, and_3_out, and_4_out);
endmodule
