// Logisim project p7.circ as structural Verilog: 2 circuits, main circuit main
module main (
  input  i0,
  input  i1,
  input  i2,
  input  i3,
  input  i4,
  input  i5,
  input  s0,
  input  i6,
  input  s2,
  input  i7,
  input  s1,
  output d
);

  _8x1_MUX u_8x1_mux_1 (
    .i0(i0), .i1(i1), .i2(i2), .i3(i3), .i4(i4), .i5(i5), .i6(i6), .i7(i7), .s2(s2), .s1(s1), .s0(s0),
    .out_12(d));
endmodule

module _8x1_MUX (
  input  i0,
  input  s2,
  input  i1,
  input  s1,
  input  i2,
  input  s0,
  input  i3,
  input  i4,
  input  i5,
  input  i6,
  input  i7,
  output out_12
);

  wire and_1_out, and_2_out, and_3_out, and_4_out, and_5_out, and_6_out, and_7_out, and_8_out, s0_prime,
       s1_prime, s2_prime;

  not not_1 (s2_prime, s2);
  not not_2 (s1_prime, s1);
  not not_3 (s0_prime, s0);
  and and_1 (and_1_out, i0, s2_prime, s1_prime, s0_prime);
  and and_2 (and_2_out, i1, s2_prime, s1_prime, s0);
  and and_3 (and_3_out, i2, s2_prime, s1, s0_prime);
  and and_4 (and_4_out, i3, s2_prime, s1, s0);
  and and_5 (and_5_out, i4, s2, s1_prime, s0_prime);
  and and_6 (and_6_out, i5, s2, s1_prime, s0);
  and and_7 (and_7_out, i6, s2, s1, s0_prime);
  and and_8 (and_8_out, i7, s2, s1, s0);
  or or_1 (out_12, and_1_out, and_2_out, and_3_out, and_4_out, and_5_out, and_6_out, and_7_out, and_8_out);
endmodule
