// Logisim project p8.circ as structural Verilog: 1 circuit, main circuit main
module main (
  input  i0,
  input  i1,
  input  s3,
  input  s2,
  input  i2,
  input  s1,
  input  i3,
  input  s0,
  input  i4,
  input  i5,
  input  i6,
  input  i7,
  input  i8,
  input  i9,
  input  i10,
  input  i11,
  input  i12,
  input  i13,
  input  i14,
  input  i15,
  output out_21
);

  wire and_1_out, and_2_out, and_3_out, and_4_out, and_5_out, and_6_out, and_7_out, and_8_out, and_9_out,
       and_10_out, and_11_out, and_12_out, and_13_out, and_14_out, and_15_out, and_16_out, s0_prime,
       s1_prime, s2_prime, s3_prime;

  not not_1 (s3_prime, s3);
  not not_2 (s2_prime, s2);
  not not_3 (s1_prime, s1);
  not not_4 (s0_prime, s0);
  and and_1 (and_1_out, i0, s3_prime, s2_prime, s1_prime, s0_prime);
  and and_2 (and_2_out, i1, s3_prime, s2_prime, s1_prime, s0);
  and and_3 (and_3_out, i2, s2_prime, s3_prime, s1, s0_prime);
  and and_4 (and_4_out, i3, s2_prime, s3_prime, s1, s0);
  and and_5 (and_5_out, i4, s2, s3_prime, s1_prime, s0_prime);
  and and_6 (and_6_out, i5, s2, s3_prime, s1_prime, s0);
  and and_7 (and_7_out, i6, s2, s3_prime, s1, s0_prime);
  and and_8 (and_8_out, i7, s2, s3_prime, s1, s0);
  and and_9 (and_9_out, i8, s3, s2_prime, s1_prime, s0_prime);
  and and_10 (and_10_out, i9, s3, s2_prime, s1_prime, s0);
  and and_11 (and_11_out, i10, s2_prime, s3, s1, s0_prime);
  and and_12 (and_12_out, i11, s2_prime, s3, s1, s0);
  and and_13 (and_13_out, i12, s2, s3, s1_prime, s0_prime);
  and and_14 (and_14_out, i13, s2, s3, s1_prime, s0);
  and and_15 (and_15_out, i14, s2, s3, s1, s0_prime);
  and and_16 (and_16_out, i15, s2, s3, s1, s0);
  or or_1 (out_21, and_1_out, and_2_out, and_3_out, and_4_out, and_5_out, and_6_out, and_7_out, and_8_out, and_9_out, and_10_out, and_11_out, and_12_out, and_13_out, and_14_out, and_15_out, and_16_out);
endmodule
