// Logisim project p9.circ as structural Verilog: 4 circuits, main circuit main
module main (
  input  a1,
  input  a0,
  input  b1,
  input  b0,
  output s1,
  output s0,
  output c
);

  wire ha_1_carry;

  HA ha_1 (.A(a0), .B(b0), .SUM(s0), .CARRY(ha_1_carry));
  FA fa_1 (.A(a1), .B(b1), .C(ha_1_carry), .SUM(s1), .CARRY(c));
endmodule

module HA (
  input  A,
  input  B,
  output SUM,
  output CARRY
);

  wire and_1_out, and_2_out, not_1_out, not_2_out;

  not not_1 (not_1_out, A);
  not not_2 (not_2_out, B);
  and and_1 (and_1_out, not_1_out, B);
  and and_2 (and_2_out, not_2_out, A);
  or or_1 (SUM, and_1_out, and_2_out);
  and and_3 (CARRY, A, B);
endmodule

module XOR (
  input  in_1,
  input  in_2,
  output out_3
);

  wire and_1_out, and_2_out, not_1_out, not_2_out;

  not not_1 (not_1_out, in_1);
  not not_2 (not_2_out, in_2);
  and and_1 (and_1_out, in_1, not_2_out);
  and and_2 (and_2_out, not_1_out, in_2);
  or or_1 (out_3, and_1_out, and_2_out);
endmodule

module FA (
  input  A,
  input  B,
  input  C,
  output SUM,
  output CARRY
);

  wire and_1_out, and_2_out, xor_1_out_3;

  XOR xor_1 (.in_1(A), .in_2(B), .out_3(xor_1_out_3));
  and and_1 (and_1_out, A, B);
  XOR xor_2 (.in_1(xor_1_out_3), .in_2(C), .out_3(SUM));
  and and_2 (and_2_out, xor_1_out_3, C);
  or or_1 (CARRY, and_2_out, and_1_out);
endmodule
