// Logisim project p1.circ as structural Verilog: 2 circuits, main circuit main
module main (
  input  c,
  input  a,
  input  b,
  output sum,
  output carry
);

  wire not_1_out;

  not not_1 (not_1_out, c);
  _4_1_MUX u_4_1_mux_1 (.i0(c), .i1(not_1_out), .i2(not_1_out), .i3(c), .s1(a), .s0(b), .d(sum));
  _4_1_MUX u_4_1_mux_2 (.i0(1'b0), .i1(c), .i2(c), .i3(1'b1), .s1(a), .s0(b), .d(carry));
endmodule

module _4_1_MUX (
  input  i0,
  input  i1,
  input  i2,
  input  i3,
  input  s1,
  input  s0,
  output d
);

  wire and_1_out, and_2_out, and_3_out, and_4_out, not_1_out, not_2_out;

  not not_1 (not_1_out, s1);
  not not_2 (not_2_out, s0);
  and and_1 (and_1_out, i0, not_1_out, not_2_out);
  and and_2 (and_2_out, i1, s0, not_1_out);
  and and_3 (and_3_out, i2, not_2_out, s1);
  and and_4 (and_4_out, i3, s1, s0);
  or or_1 (d, and_1_out, and_2_out, and_3_out, and_4_out);
endmodule
