// Logisim project p2.circ as structural Verilog: 3 circuits, main circuit main
module main (
  input  in_1,
  input  in_2,
  input  in_3,
  input  in_4,
  input  in_5,
  input  in_6,
  input  in_7,
  input  in_8,
  input  in_9,
  input  in_10,
  input  in_11,
  input  in_12,
  input  in_13,
  input  in_14,
  input  in_15,
  input  in_16,
  input  in_17,
  output out_18,
  output out_19,
  output out_20,
  output out_21,
  output out_22,
  output out_23,
  output out_24,
  output out_25,
  output out_26,
  output out_27,
  output out_28
);

  wire xor_1_out, xor_2_out;

  xor xor_1 (xor_1_out, in_13, in_9);
  xor xor_2 (xor_2_out, out_24, out_25);
  _4_bit_FA u_4_bit_fa_1 (
    .A0(in_16), .A1(in_15), .A2(in_14), .A3(in_13), .B0(in_12), .B1(in_11), .B2(in_10), .B3(in_9),
    .Cin(out_18), .S0(out_20), .S1(out_27), .S2(out_26), .S3(out_25), .C0(out_24));
  xor xor_3 (out_28, xor_2_out, xor_1_out);
  _4_bit_FA u_4_bit_fa_2 (
    .A0(in_8), .A1(in_7), .A2(in_6), .A3(in_5), .B0(in_4), .B1(in_3), .B2(in_2), .B3(in_1), .Cin(in_17),
    .S0(out_19), .S1(out_23), .S2(out_22), .S3(out_21), .C0(out_18));

  // Other names for the same wires on the sheet: C0 = out_18
endmodule

module FA (
  input  A,
  input  B,
  input  C,
  output SUM,
  output CARRY
);

  wire and_1_out, and_2_out, and_3_out, xor_1_out;

  xor xor_1 (xor_1_out, A, B);
  and and_1 (and_1_out, A, B);
  and and_2 (and_2_out, B, C);
  and and_3 (and_3_out, A, C);
  or or_1 (CARRY, and_1_out, and_2_out, and_3_out);
  xor xor_2 (SUM, xor_1_out, C);
endmodule

module _4_bit_FA (
  input  A0,
  input  A1,
  input  A2,
  input  A3,
  input  B0,
  input  B1,
  input  B2,
  input  B3,
  input  Cin,
  output S0,
  output S1,
  output S2,
  output S3,
  output C0
);

  wire fa_1_carry, fa_2_carry, fa_3_carry, xor_1_out, xor_2_out, xor_3_out, xor_4_out;

  xor xor_1 (xor_1_out, B0, Cin);
  xor xor_2 (xor_2_out, B1, Cin);
  xor xor_3 (xor_3_out, B2, Cin);
  xor xor_4 (xor_4_out, B3, Cin);
  FA fa_1 (.A(A0), .B(xor_1_out), .C(Cin), .SUM(S0), .CARRY(fa_1_carry));
  FA fa_2 (.A(A1), .B(xor_2_out), .C(fa_1_carry), .SUM(S1), .CARRY(fa_2_carry));
  FA fa_3 (.A(A2), .B(xor_3_out), .C(fa_2_carry), .SUM(S2), .CARRY(fa_3_carry));
  FA fa_4 (.A(A3), .B(xor_4_out), .C(fa_3_carry), .SUM(S3), .CARRY(C0));
endmodule
