// Logisim project ALU16.circ as structural Verilog: 1 circuit, main circuit main
module main (
  input  in_1,
  input  in_2,
  input  [15:0] A,
  input  [15:0] B,
  input  [3:0] select,
  output out_6,
  output out_7,
  output out_8,
  output [15:0] \output ,
  output [15:0] bit_17_32,
  output [15:0] remainder
);

  wire comparator_1_lt;
  wire [15:0] adder_1_out, and_1_out, bit_extender_1_out, divider_1_out, multiplier_1_out, nand_1_out,
       nor_1_out, or_1_out, subtractor_1_out, xnor_1_out, xor_1_out;

  Adder #(.width(16)) adder_1 (.a(A), .b(B), .out(adder_1_out), .cin(in_1), .cout(out_6));
  Subtractor #(.width(16)) subtractor_1 (.a(A), .b(B), .out(subtractor_1_out), .bin(in_2), .bout(out_7));
  Multiplier #(.width(16)) multiplier_1 (.a(A), .b(B), .out(multiplier_1_out), .cout(bit_17_32));  // open: cin
  Divider #(.width(16)) divider_1 (.a(A), .b(B), .out(divider_1_out), .rem(remainder));  // open: upper
  assign and_1_out = A & B;  // AND_Gate and_1, 16 bits wide
  assign or_1_out = A | B;  // OR_Gate or_1, 16 bits wide
  assign xor_1_out = A ^ B;  // XOR_Gate xor_1, 16 bits wide
  assign nand_1_out = ~(A & B);  // NAND_Gate nand_1, 16 bits wide
  assign nor_1_out = ~(A | B);  // NOR_Gate nor_1, 16 bits wide
  assign xnor_1_out = ~(A ^ B);  // XNOR_Gate xnor_1, 16 bits wide
  Comparator #(.width(16)) comparator_1 (.a(A), .b(B), .lt(comparator_1_lt));  // open: gt, eq
  assign bit_extender_1_out = {{15{1'b0}}, comparator_1_lt};  // Bit_Extender bit_extender_1
  Multiplexer #(.select(4), .width(16)) multiplexer_1 (
    .in0(adder_1_out), .in1(subtractor_1_out), .in2(multiplier_1_out), .in3(divider_1_out), .in4(and_1_out),
    .in5(or_1_out), .in6(xor_1_out), .in7(nand_1_out), .in8(nor_1_out), .in9(xnor_1_out),
    .in10(bit_extender_1_out), .out(\output ), .sel(select));  // open: in11, in12, in13, in14, in15, en
  Comparator #(.width(16)) comparator_2 (.a({16{1'b0}}), .b(\output ), .eq(out_8));  // open: gt, lt
endmodule
