// Logisim project p1.circ as structural Verilog: 6 circuits, main circuit main
module main (
  input  [3:0] A,
  input  [3:0] B,
  input  s1,
  input  s0,
  output [3:0] \output 
);

  wire [3:0] n4_bit_adder_1_s0, n4_bit_and_1_out_3, n4_bit_or_1_out_3;

  _4_bit_adder u_4_bit_adder_1 (
    .a(A), .in_3(B), .cin(s0), .s0(n4_bit_adder_1_s0[0]), .s1(n4_bit_adder_1_s0[1]),
    .s2(n4_bit_adder_1_s0[2]), .s3(n4_bit_adder_1_s0[3]));  // open: co
  _4_bit_AND u_4_bit_and_1 (
    .a(A), .in_2(B), .out_3(n4_bit_and_1_out_3[0]), .out_4(n4_bit_and_1_out_3[1]),
    .out_5(n4_bit_and_1_out_3[2]), .out_6(n4_bit_and_1_out_3[3]));
  _4_bit_OR u_4_bit_or_1 (
    .a(A), .in_2(B), .out_3(n4_bit_or_1_out_3[0]), .out_4(n4_bit_or_1_out_3[1]),
    .out_5(n4_bit_or_1_out_3[2]), .out_6(n4_bit_or_1_out_3[3]));
  Multiplexer #(.select(2), .width(4)) multiplexer_1 (
    .in0(n4_bit_adder_1_s0), .in1(n4_bit_adder_1_s0), .in2(n4_bit_and_1_out_3), .in3(n4_bit_or_1_out_3),
    .out(\output ), .sel({s1, s0}));  // open: en
endmodule

// Adder/Subtractor
module _4_bit_adder (
  input  cin,
  input  [3:0] a,
  input  [3:0] in_3,
  output s0,
  output s1,
  output s2,
  output s3,
  output co
);

  wire n1_bit_fa_1_co, n1_bit_fa_2_co, n1_bit_fa_3_co, xor_1_out, xor_2_out, xor_3_out, xor_4_out;

  xor xor_1 (xor_1_out, cin, in_3[0]);
  xor xor_2 (xor_2_out, cin, in_3[1]);
  xor xor_3 (xor_3_out, cin, in_3[2]);
  xor xor_4 (xor_4_out, cin, in_3[3]);
  _1_bit_FA u_1_bit_fa_1 (.a(a[0]), .b(xor_1_out), .cin(cin), .co(n1_bit_fa_1_co), .s(s0));
  _1_bit_FA u_1_bit_fa_2 (.a(a[1]), .b(xor_2_out), .cin(n1_bit_fa_1_co), .co(n1_bit_fa_2_co), .s(s1));
  _1_bit_FA u_1_bit_fa_3 (.a(a[2]), .b(xor_3_out), .cin(n1_bit_fa_2_co), .co(n1_bit_fa_3_co), .s(s2));
  _1_bit_FA u_1_bit_fa_4 (.a(a[3]), .b(xor_4_out), .cin(n1_bit_fa_3_co), .co(co), .s(s3));
endmodule

// AND
module _4_bit_AND (
  input  [3:0] a,
  input  [3:0] in_2,
  output out_3,
  output out_4,
  output out_5,
  output out_6
);

  and and_1 (out_3, a[0], in_2[0]);
  and and_2 (out_4, a[1], in_2[1]);
  and and_3 (out_5, a[2], in_2[2]);
  and and_4 (out_6, a[3], in_2[3]);
endmodule

// OR
module _4_bit_OR (
  input  [3:0] a,
  input  [3:0] in_2,
  output out_3,
  output out_4,
  output out_5,
  output out_6
);

  or or_1 (out_3, a[0], in_2[0]);
  or or_2 (out_4, a[1], in_2[1]);
  or or_3 (out_5, a[2], in_2[2]);
  or or_4 (out_6, a[3], in_2[3]);
endmodule

module _1_bit_FA (
  input  cin,
  input  a,
  input  b,
  output s,
  output co
);

  wire and_1_out, and_2_out, xor_1_out;

  xor xor_1 (xor_1_out, a, b);
  and and_1 (and_1_out, a, b);
  and and_2 (and_2_out, cin, xor_1_out);
  or or_1 (co, and_1_out, and_2_out);
  xor xor_2 (s, cin, xor_1_out);
endmodule

module _4_1_MUX (
  input  i0,
  input  i1,
  input  i2,
  input  i3,
  input  s1,
  input  s0,
  output out_7
);

  wire and_1_out, and_2_out, and_3_out, and_4_out, not_1_out, not_2_out;

  not not_1 (not_1_out, s1);
  not not_2 (not_2_out, s0);
  and and_1 (and_1_out, i0, not_1_out, not_2_out);
  and and_2 (and_2_out, i1, not_1_out, s0);
  and and_3 (and_3_out, i2, s1, not_2_out);
  and and_4 (and_4_out, i3, s1, s1);
  or or_1 (out_7, and_1_out, and_2_out, and_3_out, and_4_out);
endmodule
