// Logisim project p2.circ as structural Verilog: 3 circuits, main circuit main
module main (
  input  in_1,
  input  in_2,
  input  in_3,
  input  in_4,
  input  in_5,
  input  in_6,
  input  in_7,
  input  in_8,
  input  in_9,
  input  in_10,
  input  in_11,
  input  in_12,
  input  in_13,
  input  in_14,
  input  in_15,
  input  in_16,
  input  in_17,
  input  in_18,
  input  in_19,
  input  in_20,
  output out_21,
  output [3:0] out_22,
  output [3:0] out_23,
  output [3:0] out_24
);

  wire n4_bit_adder_2_co, n4_bit_adder_3_co;

  _4_bit_Adder u_4_bit_adder_1 (
    .a({2'b00, in_3, in_4}), .in_3({2'b00, in_1, in_2}), .cin(n4_bit_adder_2_co), .co(out_21),
    .s0(out_22[0]), .s1(out_22[1]), .s2(out_22[2]), .s3(out_22[3]));
  _4_bit_Adder u_4_bit_adder_2 (
    .a({in_13, in_14, in_15, in_16}), .in_3({in_5, in_6, in_7, in_8}), .cin(n4_bit_adder_3_co),
    .co(n4_bit_adder_2_co), .s0(out_23[0]), .s1(out_23[1]), .s2(out_23[2]), .s3(out_23[3]));
  _4_bit_Adder u_4_bit_adder_3 (
    .a({in_17, in_18, in_19, in_20}), .in_3({in_9, in_10, in_11, in_12}), .cin(1'b0), .co(n4_bit_adder_3_co),
    .s0(out_24[0]), .s1(out_24[1]), .s2(out_24[2]), .s3(out_24[3]));
endmodule

module _4_bit_Adder (
  input  cin,
  input  [3:0] a,
  input  [3:0] in_3,
  output s0,
  output s1,
  output s2,
  output s3,
  output co
);

  wire n1_bit_fa_1_co, n1_bit_fa_2_co, n1_bit_fa_3_co, xor_1_out, xor_2_out, xor_3_out, xor_4_out;

  xor xor_1 (xor_1_out, cin, in_3[0]);
  xor xor_2 (xor_2_out, cin, in_3[1]);
  xor xor_3 (xor_3_out, cin, in_3[2]);
  xor xor_4 (xor_4_out, cin, in_3[3]);
  _1_bit_FA u_1_bit_fa_1 (.a(a[0]), .b(xor_1_out), .cin(cin), .co(n1_bit_fa_1_co), .s(s0));
  _1_bit_FA u_1_bit_fa_2 (.a(a[1]), .b(xor_2_out), .cin(n1_bit_fa_1_co), .co(n1_bit_fa_2_co), .s(s1));
  _1_bit_FA u_1_bit_fa_3 (.a(a[2]), .b(xor_3_out), .cin(n1_bit_fa_2_co), .co(n1_bit_fa_3_co), .s(s2));
  _1_bit_FA u_1_bit_fa_4 (.a(a[3]), .b(xor_4_out), .cin(n1_bit_fa_3_co), .co(co), .s(s3));
endmodule

module _1_bit_FA (
  input  cin,
  input  a,
  input  b,
  output s,
  output co
);

  wire and_1_out, and_2_out, xor_1_out;

  xor xor_1 (xor_1_out, a, b);
  and and_1 (and_1_out, a, b);
  and and_2 (and_2_out, cin, xor_1_out);
  or or_1 (co, and_1_out, and_2_out);
  xor xor_2 (s, cin, xor_1_out);
endmodule
