// Logisim project lab8.circ as structural Verilog: 1 circuit, main circuit main
module main (
  input  in_1,
  input  in_2
);

  wire clock_1_out;
  wire [3:0] t_ff_1_q;

  Clock clock_1 (.out(clock_1_out));
  Hex_Digit_Display hex_digit_display_1 (.value(t_ff_1_q));  // open: dp
  T_Flip_Flop t_ff_1 (.clk(clock_1_out), .T(in_1), .Q(t_ff_1_q[0]), .reset(in_2));  // open: Qn, preset, en
  LED led_1 (.in(t_ff_1_q[0]));
  T_Flip_Flop t_ff_2 (.clk(t_ff_1_q[0]), .T(in_1), .Q(t_ff_1_q[1]), .reset(in_2));  // open: Qn, preset, en
  T_Flip_Flop t_ff_3 (.clk(t_ff_1_q[1]), .T(in_1), .Q(t_ff_1_q[2]), .reset(in_2));  // open: Qn, preset, en
  LED led_2 (.in(t_ff_1_q[1]));
  T_Flip_Flop t_ff_4 (.clk(t_ff_1_q[2]), .T(in_1), .Q(t_ff_1_q[3]), .reset(in_2));  // open: Qn, preset, en
  LED led_3 (.in(t_ff_1_q[3]));
  LED led_4 (.in(t_ff_1_q[2]));
endmodule
