// Logisim project p0.circ as structural Verilog: 1 circuit, main circuit main
module main (
  input  S,
  input  J,
  input  R,
  input  K,
  input  Preset,
  input  Preset_2,
  input  Enable,
  input  Enable_2,
  input  Clear,
  input  Clear_2,
  input  in_11,
  input  D,
  input  in_13,
  input  Preset_3,
  input  in_15,
  input  Enable_3,
  input  in_17,
  input  Clear_3
);

  wire Clock_2_out, Clock_3_out, Clock_4_out, Clock_out, d_ff_1_q, j_k_ff_1_q, s_r_ff_1_q, t_ff_1_q;

  Clock Clock (.out(Clock_out));
  Clock Clock_2 (.out(Clock_2_out));
  S_R_Flip_Flop s_r_ff_1 (
    .S(S), .clk(Clock_out), .R(R), .Q(s_r_ff_1_q), .preset(Preset), .reset(Clear), .en(Enable));  // open: Qn
  T_Flip_Flop t_ff_1 (
    .clk(Clock_2_out), .T(in_11), .Q(t_ff_1_q), .preset(in_13), .reset(in_17), .en(in_15));  // open: Qn
  LED led_1 (.in(t_ff_1_q));
  LED led_2 (.in(s_r_ff_1_q));
  Clock Clock_3 (.out(Clock_3_out));
  Clock Clock_4 (.out(Clock_4_out));
  D_Flip_Flop d_ff_1 (
    .clk(Clock_4_out), .D(D), .Q(d_ff_1_q), .preset(Preset_3), .en(Enable_3), .reset(Clear_3));  // open: Qn
  J_K_Flip_Flop j_k_ff_1 (
    .J(J), .clk(Clock_3_out), .K(K), .Q(j_k_ff_1_q), .preset(Preset_2), .en(Enable_2), .reset(Clear_2));  // open: Qn
  LED led_3 (.in(j_k_ff_1_q));
  LED led_4 (.in(d_ff_1_q));

  // Notes on the sheet:
  //   SR Flip Flop
  //   T Flip Flop
  //   JK Flip Flop
  //   D Flip Flop
endmodule
