// Logisim project p1.circ as structural Verilog: 1 circuit, main circuit main
module main (
  input  Enable,
  input  shr_in,
  output Q7,
  output Q6,
  output Q5,
  output Q4,
  output Q3,
  output Q2,
  output Q1,
  output Q0
);

  wire Clock_out;

  Clock Clock (.out(Clock_out));
  Register #(.width(1)) register_1 (.D(Q6), .en(Enable), .Q(Q7), .clk(Clock_out));  // open: clr
  Register #(.width(1)) register_2 (.D(Q5), .en(Enable), .Q(Q6), .clk(Clock_out));  // open: clr
  Register #(.width(1)) register_3 (.D(Q4), .en(Enable), .Q(Q5), .clk(Clock_out));  // open: clr
  Register #(.width(1)) register_4 (.D(Q3), .en(Enable), .Q(Q4), .clk(Clock_out));  // open: clr
  Register #(.width(1)) register_5 (.D(Q2), .en(Enable), .Q(Q3), .clk(Clock_out));  // open: clr
  Register #(.width(1)) register_6 (.D(Q1), .en(Enable), .Q(Q2), .clk(Clock_out));  // open: clr
  Register #(.width(1)) register_7 (.D(Q0), .en(Enable), .Q(Q1), .clk(Clock_out));  // open: clr
  Register #(.width(1)) register_8 (.D(shr_in), .en(Enable), .Q(Q0), .clk(Clock_out));  // open: clr

  // Notes on the sheet:
  //   8-bit Shift Register
endmodule
