// Logisim project p3.circ as structural Verilog: 1 circuit, main circuit main
// 4-bit counter
module main (
  input  in_1,
  input  in_2,
  input  in_3,
  input  in_4
);

  wire clock_1_out, clock_2_out;
  wire [1:0] t_ff_9_q;
  wire [3:0] t_ff_1_q, t_ff_2_q;

  Clock clock_1 (.out(clock_1_out));
  Hex_Digit_Display hex_digit_display_1 (.value({2'b00, t_ff_9_q}));  // open: dp
  Clock clock_2 (.out(clock_2_out));
  Hex_Digit_Display hex_digit_display_2 (.value(t_ff_2_q));  // open: dp
  T_Flip_Flop t_ff_1 (.clk(clock_1_out), .T(in_3), .Q(t_ff_1_q[0]), .reset(in_4));  // open: Qn, preset, en
  LED led_1 (.in(t_ff_1_q[0]));
  Hex_Digit_Display hex_digit_display_3 (.value(t_ff_1_q));  // open: dp
  T_Flip_Flop t_ff_2 (.clk(clock_2_out), .T(in_1), .Q(t_ff_2_q[0]), .reset(in_2));  // open: Qn, preset, en
  LED led_2 (.in(t_ff_2_q[0]));
  T_Flip_Flop t_ff_3 (.clk(t_ff_1_q[0]), .T(in_3), .Q(t_ff_1_q[1]), .reset(in_4));  // open: Qn, preset, en
  T_Flip_Flop t_ff_4 (.clk(t_ff_2_q[0]), .T(in_1), .Q(t_ff_2_q[1]), .reset(in_2));  // open: Qn, preset, en
  LED led_3 (.in(t_ff_1_q[1]));
  T_Flip_Flop t_ff_5 (.clk(t_ff_2_q[1]), .T(in_1), .Q(t_ff_2_q[2]), .reset(in_2));  // open: Qn, preset, en
  LED led_4 (.in(t_ff_2_q[1]));
  T_Flip_Flop t_ff_6 (.clk(t_ff_1_q[1]), .T(in_3), .Q(t_ff_1_q[2]), .reset(in_4));  // open: Qn, preset, en
  LED led_5 (.in(t_ff_1_q[2]));
  LED led_6 (.in(t_ff_2_q[2]));
  T_Flip_Flop t_ff_7 (.clk(t_ff_1_q[2]), .T(in_3), .Q(t_ff_1_q[3]), .reset(in_4));  // open: Qn, preset, en
  LED led_7 (.in(t_ff_1_q[3]));
  T_Flip_Flop t_ff_8 (.clk(t_ff_2_q[2]), .T(in_1), .Q(t_ff_2_q[3]), .reset(in_2));  // open: Qn, preset, en
  LED led_8 (.in(t_ff_2_q[3]));
  T_Flip_Flop t_ff_9 (.clk(t_ff_1_q[3]), .T(in_3), .Q(t_ff_9_q[0]), .reset(in_4));  // open: Qn, preset, en
  LED led_9 (.in(t_ff_9_q[0]));
  T_Flip_Flop t_ff_10 (.clk(t_ff_9_q[0]), .T(in_3), .Q(t_ff_9_q[1]), .reset(in_4));  // open: Qn, preset, en
  LED led_10 (.in(t_ff_9_q[1]));

  // Notes on the sheet:
  //   4-bit Counter
  //   6-bit Counter
endmodule
