// Logisim project p4.circ as structural Verilog: 2 circuits, main circuit main
module main (
  input  i0,
  input  i1,
  input  i2,
  input  i3,
  input  i4,
  input  i5,
  input  i6,
  input  i7,
  input  shr_in,
  input  [1:0] in_10,
  output Q0,
  output Q1,
  output Q2,
  output Q3,
  output Q4,
  output Q5,
  output Q6,
  output Q7
);

  wire clock_1_out, multiplexer_1_out, multiplexer_2_out, multiplexer_3_out, multiplexer_4_out,
       multiplexer_5_out, multiplexer_6_out, multiplexer_7_out, multiplexer_8_out;

  Clock clock_1 (.out(clock_1_out));
  Multiplexer #(.select(2)) multiplexer_1 (
    .in0(Q0), .in1(i0), .in2(Q1), .in3(1'b0), .out(multiplexer_1_out), .sel(in_10));  // open: en
  Multiplexer #(.select(2)) multiplexer_2 (
    .in0(Q1), .in1(i1), .in2(Q2), .in3(1'b0), .out(multiplexer_2_out), .sel(in_10));  // open: en
  Multiplexer #(.select(2), .enable("false")) multiplexer_3 (
    .in0(Q2), .in1(i2), .in2(Q3), .in3(1'b0), .out(multiplexer_3_out), .sel(in_10));
  Multiplexer #(.select(2), .enable("false")) multiplexer_4 (
    .in0(Q3), .in1(i3), .in2(Q4), .in3(1'b0), .out(multiplexer_4_out), .sel(in_10));
  Multiplexer #(.select(2)) multiplexer_5 (
    .in0(Q4), .in1(i4), .in2(Q5), .in3(1'b0), .out(multiplexer_5_out), .sel(in_10));  // open: en
  Multiplexer #(.select(2)) multiplexer_6 (
    .in0(Q5), .in1(i5), .in2(Q6), .in3(1'b0), .out(multiplexer_6_out), .sel(in_10));  // open: en
  Multiplexer #(.select(2), .enable("false")) multiplexer_7 (
    .in0(Q6), .in1(i6), .in2(Q7), .in3(1'b0), .out(multiplexer_7_out), .sel(in_10));
  Multiplexer #(.select(2), .enable("false")) multiplexer_8 (
    .in0(Q7), .in1(i7), .in2(shr_in), .in3(1'b0), .out(multiplexer_8_out), .sel(in_10));
  D_Flip_Flop d_ff_1 (.clk(clock_1_out), .D(multiplexer_1_out), .Q(Q0), .en(1'b1));  // open: Qn, preset, reset
  D_Flip_Flop d_ff_2 (.clk(clock_1_out), .D(multiplexer_2_out), .Q(Q1), .en(1'b1));  // open: Qn, preset, reset
  D_Flip_Flop d_ff_3 (.clk(clock_1_out), .D(multiplexer_3_out), .Q(Q2), .en(1'b1));  // open: Qn, preset, reset
  D_Flip_Flop d_ff_4 (.clk(clock_1_out), .D(multiplexer_4_out), .Q(Q3), .en(1'b1));  // open: Qn, preset, reset
  D_Flip_Flop d_ff_5 (.clk(clock_1_out), .D(multiplexer_5_out), .Q(Q4), .en(1'b1));  // open: Qn, preset, reset
  D_Flip_Flop d_ff_6 (.clk(clock_1_out), .D(multiplexer_6_out), .Q(Q5), .en(1'b1));  // open: Qn, preset, reset
  D_Flip_Flop d_ff_7 (.clk(clock_1_out), .D(multiplexer_7_out), .Q(Q6), .en(1'b1));  // open: Qn, preset, reset
  D_Flip_Flop d_ff_8 (.clk(clock_1_out), .D(multiplexer_8_out), .Q(Q7), .en(1'b1));  // open: Qn, preset, reset

  // Notes on the sheet:
  //   8-bit Multi Function Shift Register
endmodule

module _4_bit_Multi_Function_Shift_Register (
  input  i0,
  input  i1,
  input  i2,
  input  i3,
  input  shr_in,
  input  [1:0] in_6,
  output out_7,
  output out_8,
  output out_9,
  output out_10
);

  wire clock_1_out, multiplexer_1_out, multiplexer_2_out, multiplexer_3_out, multiplexer_4_out;

  Clock clock_1 (.out(clock_1_out));
  Multiplexer #(.select(2)) multiplexer_1 (
    .in0(out_7), .in1(i0), .in2(out_8), .in3(1'b0), .out(multiplexer_1_out), .sel(in_6));  // open: en
  Multiplexer #(.select(2)) multiplexer_2 (
    .in0(out_8), .in1(i1), .in2(out_9), .in3(1'b0), .out(multiplexer_2_out), .sel(in_6));  // open: en
  Multiplexer #(.select(2), .enable("false")) multiplexer_3 (
    .in0(out_9), .in1(i2), .in2(out_10), .in3(1'b0), .out(multiplexer_3_out), .sel(in_6));
  Multiplexer #(.select(2), .enable("false")) multiplexer_4 (
    .in0(out_10), .in1(i3), .in2(shr_in), .in3(1'b0), .out(multiplexer_4_out), .sel(in_6));
  D_Flip_Flop d_ff_1 (.clk(clock_1_out), .D(multiplexer_1_out), .Q(out_7), .en(1'b1));  // open: Qn, preset, reset
  D_Flip_Flop d_ff_2 (.clk(clock_1_out), .D(multiplexer_2_out), .Q(out_8), .en(1'b1));  // open: Qn, preset, reset
  D_Flip_Flop d_ff_3 (.clk(clock_1_out), .D(multiplexer_3_out), .Q(out_9), .en(1'b1));  // open: Qn, preset, reset
  D_Flip_Flop d_ff_4 (.clk(clock_1_out), .D(multiplexer_4_out), .Q(out_10), .en(1'b1));  // open: Qn, preset, reset

  // Notes on the sheet:
  //   4-bit Multi Function Shift Register
endmodule
