// Logisim project L9Q1_D.circ as structural Verilog: 1 circuit, main circuit main
module main (
  input  Enable,
  input  Clear,
  output Q0,
  output Q1,
  output Q2,
  output Q3
);

  wire and_1_out, and_2_out, Clock_out, d_ff_1_qn, xor_1_out, xor_2_out, xor_3_out;

  Clock Clock (.out(Clock_out));
  D_Flip_Flop d_ff_1 (
    .clk(Clock_out), .D(d_ff_1_qn), .Q(Q0), .Qn(d_ff_1_qn), .en(Enable), .reset(Clear));  // open: preset
  D_Flip_Flop d_ff_2 (.clk(Clock_out), .D(xor_1_out), .Q(Q1), .en(Enable), .reset(Clear));  // open: Qn, preset
  xor xor_1 (xor_1_out, Q0, Q1);
  and and_1 (and_1_out, Q1, Q0);
  LED MSB__Q3 (.in(Q3));
  D_Flip_Flop d_ff_3 (.clk(Clock_out), .D(xor_2_out), .Q(Q2), .en(Enable), .reset(Clear));  // open: Qn, preset
  xor xor_2 (xor_2_out, and_1_out, Q2);
  LED LSB__Q0 (.in(Q0));
  LED u_Q1 (.in(Q1));
  LED u_Q2 (.in(Q2));
  and and_2 (and_2_out, Q2, and_1_out);
  D_Flip_Flop d_ff_4 (.clk(Clock_out), .D(xor_3_out), .Q(Q3), .en(Enable), .reset(Clear));  // open: Qn, preset
  xor xor_3 (xor_3_out, and_2_out, Q3);
  Hex_Digit_Display hex_digit_display_1 (.value({Q3, Q2, Q1, Q0}));  // open: dp

  // Notes on the sheet:
  //   D0
endmodule
