// Logisim project L9Q1_JK.circ as structural Verilog: 1 circuit, main circuit main
module main (
  input  Enable,
  input  Clear,
  output Q0,
  output Q1,
  output Q2,
  output Q3
);

  wire and_1_out, and_2_out, Clock_out;

  Clock Clock (.out(Clock_out));
  J_K_Flip_Flop j_k_ff_1 (.J(1'b1), .clk(Clock_out), .K(1'b1), .Q(Q0), .en(Enable), .reset(Clear));  // open: Qn, preset
  J_K_Flip_Flop j_k_ff_2 (.J(Q0), .clk(Clock_out), .K(Q0), .Q(Q1), .en(Enable), .reset(Clear));  // open: Qn, preset
  and and_1 (and_1_out, Q1, Q0);
  LED MSB__Q0 (.in(Q0));
  LED u_Q1 (.in(Q1));
  LED u_Q2 (.in(Q2));
  LED MSB__Q3 (.in(Q3));
  J_K_Flip_Flop j_k_ff_3 (
    .J(and_1_out), .clk(Clock_out), .K(and_1_out), .Q(Q2), .en(Enable), .reset(Clear));  // open: Qn, preset
  and and_2 (and_2_out, Q2, and_1_out);
  J_K_Flip_Flop j_k_ff_4 (
    .J(and_2_out), .clk(Clock_out), .K(and_2_out), .Q(Q3), .en(Enable), .reset(Clear));  // open: Qn, preset
  Hex_Digit_Display hex_digit_display_1 (.value({Q3, Q2, Q1, Q0}));  // open: dp

  // Notes on the sheet:
  //   K0
endmodule
