// Logisim project L9Q1_SR.circ as structural Verilog: 1 circuit, main circuit main
module main (
  input  Enable,
  input  Clear,
  output Q0,
  output Q1,
  output Q2,
  output Q3
);

  wire and_1_out, and_2_out, and_3_out, and_4_out, and_5_out, and_6_out, Clock_out, s_r_ff_1_qn, s_r_ff_2_qn,
       s_r_ff_3_qn, s_r_ff_4_qn;

  Clock Clock (.out(Clock_out));
  S_R_Flip_Flop s_r_ff_1 (
    .S(s_r_ff_1_qn), .clk(Clock_out), .R(Q0), .Q(Q0), .Qn(s_r_ff_1_qn), .reset(Clear), .en(Enable));  // open: preset
  and and_1 (and_1_out, Q0, s_r_ff_2_qn);
  and and_2 (and_2_out, Q0, Q1);
  LED MSB__Q3 (.in(Q3));
  LED u_Q2 (.in(Q2));
  S_R_Flip_Flop s_r_ff_2 (
    .S(and_1_out), .clk(Clock_out), .R(and_2_out), .Q(Q1), .Qn(s_r_ff_2_qn), .reset(Clear), .en(Enable));  // open: preset
  LED u_Q1 (.in(Q1));
  LED LSB__Q0 (.in(Q0));
  and and_3 (and_3_out, and_2_out, s_r_ff_3_qn);
  and and_4 (and_4_out, and_2_out, Q2);
  Hex_Digit_Display hex_digit_display_1 (.value({Q3, Q2, Q1, Q0}));  // open: dp
  S_R_Flip_Flop s_r_ff_3 (
    .S(and_3_out), .clk(Clock_out), .R(and_4_out), .Q(Q2), .Qn(s_r_ff_3_qn), .reset(Clear), .en(Enable));  // open: preset
  and and_5 (and_5_out, and_4_out, s_r_ff_4_qn);
  and and_6 (and_6_out, and_4_out, Q3);
  S_R_Flip_Flop s_r_ff_4 (
    .S(and_5_out), .clk(Clock_out), .R(and_6_out), .Q(Q3), .Qn(s_r_ff_4_qn), .reset(Clear), .en(Enable));  // open: preset
endmodule
