// Logisim project L9Q1_T.circ as structural Verilog: 1 circuit, main circuit main
module main (
  input  Enable,
  input  Clear,
  output Q0,
  output Q1,
  output Q2,
  output Q3
);

  wire and_1_out, and_2_out, Clock_out;

  Clock Clock (.out(Clock_out));
  T_Flip_Flop t_ff_1 (.clk(Clock_out), .T(1'b1), .Q(Q0), .reset(Clear), .en(Enable));  // open: Qn, preset
  T_Flip_Flop t_ff_2 (.clk(Clock_out), .T(Q0), .Q(Q1), .reset(Clear), .en(Enable));  // open: Qn, preset
  and and_1 (and_1_out, Q1, Q0);
  T_Flip_Flop t_ff_3 (.clk(Clock_out), .T(and_1_out), .Q(Q2), .reset(Clear), .en(Enable));  // open: Qn, preset
  LED MSB__Q3 (.in(Q3));
  T_Flip_Flop t_ff_4 (.clk(Clock_out), .T(and_2_out), .Q(Q3), .reset(Clear), .en(Enable));  // open: Qn, preset
  and and_2 (and_2_out, Q2, and_1_out);
  LED u_Q1 (.in(Q1));
  LED LSB__Q0 (.in(Q0));
  LED u_Q2 (.in(Q2));
  Hex_Digit_Display hex_digit_display_1 (.value({Q3, Q2, Q1, Q0}));  // open: dp

  // Notes on the sheet:
  //   T0
endmodule
