// Logisim project Q3.circ as structural Verilog: 3 circuits, main circuit main
module main (
  input  [3:0] RA1,
  input  [3:0] RA2,
  input  [3:0] WA,
  input  [1:0] in_4,
  input  [15:0] Data_in,
  input  sel,
  input  regWrite,
  input  regRead,
  input  regClear,
  output [15:0] out_10,
  output [15:0] out_11
);

  wire CLK_out;
  wire [15:0] alu_1_result, multiplexer_1_out;

  Clock CLK (.out(CLK_out));
  Multiplexer #(.width(16)) multiplexer_1 (
    .in0(Data_in), .in1(alu_1_result), .out(multiplexer_1_out), .sel(sel));  // open: en
  _16x16_file u_16x16_file_1 (
    .R1_addr(RA1), .R2_addr(RA2), .W_addr(WA), .Data_in(multiplexer_1_out), .Clock(CLK_out),
    .regWrite(regWrite), .regRead(regRead), .regClear(regClear), .Value_1(out_10), .Value_2(out_11));
  ALU alu_1 (.IP_1(out_10), .IP_2(out_11), .SELECT(in_4), .RESULT(alu_1_result));
  Hex_Digit_Display hex_digit_display_1 (.value(out_10[15:12]));  // open: dp
  Hex_Digit_Display hex_digit_display_2 (.value(out_11[15:12]));  // open: dp
  Hex_Digit_Display hex_digit_display_3 (.value(out_10[7:4]));  // open: dp
  Hex_Digit_Display hex_digit_display_4 (.value(out_10[11:8]));  // open: dp
  Hex_Digit_Display hex_digit_display_5 (.value(out_11[11:8]));  // open: dp
  Hex_Digit_Display hex_digit_display_6 (.value(out_11[7:4]));  // open: dp
  Hex_Digit_Display hex_digit_display_7 (.value(out_10[3:0]));  // open: dp
  Hex_Digit_Display hex_digit_display_8 (.value(out_11[3:0]));  // open: dp

  // Notes on the sheet:
  //   Register File
  //   ALU
  //   Number to add
  //   Current Sum
endmodule

module _16x16_file (
  input  [3:0] R1_addr,
  input  [3:0] R2_addr,
  input  Clock,
  input  [3:0] W_addr,
  input  regWrite,
  input  [15:0] Data_in,
  input  regRead,
  input  regClear,
  output [15:0] Value_1,
  output [15:0] Value_2
);

  wire and_1_out, and_2_out, and_3_out, and_4_out, and_5_out, and_6_out, and_7_out, and_8_out, and_9_out,
       and_10_out, and_11_out, decoder_1_out1, decoder_1_out2, decoder_1_out3, decoder_1_out4,
       decoder_1_out5, decoder_1_out6, decoder_1_out7, decoder_1_out8, decoder_1_out9, decoder_1_out10,
       decoder_1_out11;
  wire [15:0] register_1_q, register_2_q, register_3_q, register_4_q, register_5_q, register_6_q,
       register_7_q, register_8_q, register_9_q, register_10_q, register_11_q;

  Decoder #(.select(4)) decoder_1 (
    .out1(decoder_1_out1), .out2(decoder_1_out2), .out3(decoder_1_out3), .out4(decoder_1_out4),
    .out5(decoder_1_out5), .out6(decoder_1_out6), .out7(decoder_1_out7), .out8(decoder_1_out8),
    .out9(decoder_1_out9), .out10(decoder_1_out10), .out11(decoder_1_out11), .sel(W_addr));  // open: out0, out12, out13, out14, out15, en
  and and_1 (and_1_out, decoder_1_out1, regWrite);
  and and_2 (and_2_out, decoder_1_out2, regWrite);
  and and_3 (and_3_out, decoder_1_out3, regWrite);
  and and_4 (and_4_out, decoder_1_out4, regWrite);
  and and_5 (and_5_out, regWrite, decoder_1_out5);
  and and_6 (and_6_out, decoder_1_out6, regWrite);
  and and_7 (and_7_out, decoder_1_out7, regWrite);
  and and_8 (and_8_out, decoder_1_out8, regWrite);
  and and_9 (and_9_out, regWrite, decoder_1_out9);
  and and_10 (and_10_out, regWrite, decoder_1_out10);
  and and_11 (and_11_out, regWrite, decoder_1_out11);
  Register #(.width(16)) register_1 (.D(Data_in), .en(and_1_out), .Q(register_1_q), .clk(Clock), .clr(regClear));
  Register #(.width(16)) register_2 (.D(Data_in), .en(and_2_out), .Q(register_2_q), .clk(Clock), .clr(regClear));
  Register #(.width(16)) register_3 (.D(Data_in), .en(and_3_out), .Q(register_3_q), .clk(Clock), .clr(regClear));
  Register #(.width(16)) register_4 (.D(Data_in), .en(and_4_out), .Q(register_4_q), .clk(Clock), .clr(regClear));
  Register #(.width(16)) register_5 (.D(Data_in), .en(and_5_out), .Q(register_5_q), .clk(Clock), .clr(regClear));
  Register #(.width(16)) register_6 (.D(Data_in), .en(and_6_out), .Q(register_6_q), .clk(Clock), .clr(regClear));
  Register #(.width(16)) register_7 (.D(Data_in), .en(and_7_out), .Q(register_7_q), .clk(Clock), .clr(regClear));
  Register #(.width(16)) register_8 (.D(Data_in), .en(and_8_out), .Q(register_8_q), .clk(Clock), .clr(regClear));
  Register #(.width(16)) register_9 (.D(Data_in), .en(and_9_out), .Q(register_9_q), .clk(Clock), .clr(regClear));
  Register #(.width(16)) register_10 (.D(Data_in), .en(and_10_out), .Q(register_10_q), .clk(Clock), .clr(regClear));
  Register #(.width(16)) register_11 (.D(Data_in), .en(and_11_out), .Q(register_11_q), .clk(Clock), .clr(regClear));
  Multiplexer #(.select(4), .width(16)) multiplexer_1 (
    .in0({16{1'b0}}), .in1(register_1_q), .in2(register_2_q), .in3(register_3_q), .in4(register_4_q),
    .in5(register_5_q), .in6(register_6_q), .in7(register_7_q), .in8(register_8_q), .in9(register_9_q),
    .in10(register_10_q), .in11(register_11_q), .in12({16{1'b0}}), .in13({16{1'b0}}), .in14({16{1'b0}}),
    .in15({16{1'b0}}), .out(Value_1), .sel(R1_addr), .en(regRead));
  Multiplexer #(.select(4), .width(16)) multiplexer_2 (
    .in0({16{1'b0}}), .in1(register_1_q), .in2(register_2_q), .in3(register_3_q), .in4(register_4_q),
    .in5(register_5_q), .in6(register_6_q), .in7(register_7_q), .in8(register_8_q), .in9(register_9_q),
    .in10(register_10_q), .in11(register_11_q), .in12({16{1'b0}}), .in13({16{1'b0}}), .in14({16{1'b0}}),
    .in15({16{1'b0}}), .out(Value_2), .sel(R2_addr), .en(regRead));

  // Other names for the same wires on the sheet: R_enable = regRead
endmodule

module ALU (
  input  [15:0] IP_1,
  input  [15:0] IP_2,
  input  [1:0] SELECT,
  output [15:0] RESULT
);

  wire [15:0] adder_1_out, and_1_out, or_1_out, subtractor_1_out;

  assign and_1_out = IP_1 & IP_2;  // AND_Gate and_1, 16 bits wide
  assign or_1_out = IP_1 | IP_2;  // OR_Gate or_1, 16 bits wide
  Adder #(.width(16)) adder_1 (.a(IP_1), .b(IP_2), .out(adder_1_out), .cin(1'b0));  // open: cout
  Subtractor #(.width(16)) subtractor_1 (.a(IP_1), .b(IP_2), .out(subtractor_1_out), .bin(1'b0));  // open: bout
  Multiplexer #(.select(2), .width(16)) multiplexer_1 (
    .in0(adder_1_out), .in1(subtractor_1_out), .in2(and_1_out), .in3(or_1_out), .out(RESULT), .sel(SELECT));  // open: en
endmodule
